// Digital circuit cpu-32 test.dig as structural Verilog
module cpu_32_test (
  input  E,
  input  [31:0] I_D__bus,
  input  [31:0] D_D__bus,
  input  [31:0] I_A__bus,
  input  [31:0] D_A__bus,
  input  INT_nor,
  input  INT_nmk,
  input  run,
  input  I_valid,
  input  D_accept,
  input  C,
  input  [31:0] INT_vec,
  input  B_used,
  input  [31:0] MMU_abs,
  output I_LD,
  output D_LD,
  output D_ST,
  output MMU_dis,
  output MMU_en,
  output INT_str,
  output [1:0] CSH_mode,
  output CSH_run,
  output INT_out,
  output [1:0] D_MD,
  output [31:0] MMU_base
);

  wire alu_32_1_p6, alu_32_1_p9, ALU_A_CLR, ALU_A_CMP, ALU_A_DRD, ALU_A_DRE, ALU_A_FRD, ALU_A_FRE, ALU_A_LD,
       ALU_A_LRD, ALU_A_STD, ALU_A_STF, ALU_A_UUD, ALU_A_UUF, ALU_A_V, ALU_A_VD, ALU_A_VF, ALU_B_CLR,
       ALU_B_CMP, ALU_B_DRD, ALU_B_DRE, ALU_B_FRD, ALU_B_FRE, ALU_B_LD, ALU_B_LRD, ALU_B_STD, ALU_B_STF,
       ALU_B_UUD, ALU_B_UUF, ALU_B_V, ALU_B_VD, ALU_B_VF, ALU_busy, ALU_free, and_1_out, and_3_out,
       and_4_out, and_5_out, and_6_out, and_7_out, and_8_out, and_9_out, and_10_out, and_11_out, and_12_out,
       and_13_out, and_14_out, and_15_out, and_16_out, and_17_out, and_18_out, and_20_out, and_21_out,
       and_22_out, and_23_out, and_25_out, and_26_out, and_27_out, and_32_out, and_33_out, and_34_out,
       and_37_out, and_38_out, and_39_out, and_40_out, and_41_out, and_43_out, and_44_out, and_45_out,
       and_46_out, and_47_out, and_48_out, and_49_out, and_50_out, and_51_out, and_52_out, and_53_out,
       and_54_out, and_55_out, and_56_out, and_57_out, and_60_out, and_63_out, and_64_out, and_65_out,
       and_66_out, and_67_out, and_68_out, and_69_out, and_70_out, and_71_out, and_72_out, and_73_out,
       and_74_out, and_75_out, and_76_out, and_77_out, and_80_out, and_81_out, and_85_out, and_86_out,
       and_87_out, and_88_out, and_89_out, and_90_out, and_91_out, and_92_out, and_93_out, and_94_out,
       and_95_out, and_96_out, and_98_out, and_99_out, and_102_out, and_103_out, and_108_out, and_114_out,
       and_115_out, and_116_out, and_117_out, and_118_out, and_119_out, and_120_out, and_121_out,
       and_122_out, and_123_out, and_124_out, and_125_out, and_126_out, and_129_out, and_131_out,
       and_132_out, and_137_out, and_138_out, and_139_out, and_140_out, and_141_out, and_142_out,
       and_145_out, and_146_out, and_147_out, and_148_out, and_150_out, and_151_out, and_152_out,
       and_153_out, and_155_out, and_156_out, and_157_out, and_158_out, and_159_out, and_160_out,
       and_161_out, and_167_out, and_168_out, and_171_out, and_172_out, and_173_out, and_174_out,
       and_175_out, and_176_out, and_177_out, and_181_out, and_186_out, and_188_out, and_189_out,
       and_190_out, and_191_out, and_192_out, and_193_out, and_194_out, and_195_out, and_196_out,
       and_198_out, and_199_out, and_200_out, and_201_out, and_206_out, bitselector_1_out, BTB_JP,
       BTB_override, C_ct, C_dt, clr, clr_ep, clr_sel, clrs_ep, com1, com1_ep, com1_M, com2, com2_ep,
       comparator_1_eq, comparator_2_eq, comparator_3_gt, comparator_4_eq, comparator_5_eq, comparator_6_eq,
       comparator_7_gt, comparator_8_eq, comparator_9_eq, comparator_10_eq, comparator_11_eq,
       comparator_12_eq, comparator_13_eq, comparator_14_eq, comparator_15_eq, comparator_16_eq,
       comparator_17_eq, comparator_18_gt, comparator_18_lt, comparator_19_eq, comparator_20_eq,
       comparator_21_eq, comparator_22_eq, CT_ALU__LD, CT_ALU__M, CT_ALU__M2, CT_ALU__WD, CT_ALU__WF,
       CT_BLOCK, CT_BUS__DAG, CT_BUS__DAM, CT_BUS__DAR, CT_BUS__DDG, CT_BUS__DDM, CT_BUS__DDR, CT_BUS__IAG,
       CT_BUS__IAR, CT_BUS__IDM, CT_BUS__IDR, CT_CALL__LD, CT_CALLM, CT_DIR__EXM, CT_DIR__LD, CT_DIR__M,
       CT_DIR__MS, CT_DISP, CT_FL__W1, CT_FL__W2, CT_FU__EPOCH, CT_FU__EX, CT_FU__MF, CT_INT, CT_INT__W,
       CT_INTM, CT_ISCCM, CT_ISCE, CT_ISCSM, CT_ISS__HALT, CT_ISS__OFL, CT_ISS__OLDB, CT_ISS__ORC,
       CT_ISS__OSC, CT_ISS__OSTB, CT_ISS__UFL, CT_ISS__UMM, CT_ISS__URA, CT_ISS__URB, CT_JPU__JP, CT_JPU__LD,
       CT_KILL, CT_LDB__LD, CT_MB__LD, CT_MB__OFFM, CT_MB__ST, CT_MVR, CT_PVECE, CT_RET__LD, CT_RF__DM,
       CT_RF__E, CT_RF__EX1, CT_RF__EX2, CT_RF__FLS, CT_RF__PCAE, CT_RF__PCH, CT_RF__PCJ, CT_RF__PCR,
       CT_RF__PCSE, CT_RF__SCAE, CT_RF__SCD, CT_RF__SCSE, CT_RF__SCSRE, CT_RF__SCSS, CT_RF__W1, CT_RF__W2,
       CT_ROB__EX__E, CT_ROB__FL__STA, CT_ROB__FL__STB, CT_ROB__GEN__STA, CT_ROB__GEN__STB, CT_ROB__INT__STA,
       CT_ROB__INT__STB, CT_ROB__ST__E, CT_rollback, CT_SC__W1, CT_SC__W2, CT_STB__LD, CT_TRAP__LD, CT_UBTB,
       CT_USCB, d_ff_1_q, d_ff_2_q, d_ff_18_q, d_ff_19_nq, d_ff_24_q, DC_B_q, dc_e, DC_q, dipswitch_1_out,
       dipswitch_2_out, dipswitch_3_out, dipswitch_4_out, dipswitch_5_out, dipswitch_6_out, dipswitch_7_out,
       dipswitch_8_out, dipswitch_9_out, dipswitch_10_out, dipswitch_11_out, dipswitch_12_out,
       dipswitch_13_out, DIR_busy, DIR_CLR, DIR_EX, DIR_free, DIR_LD, DIR_RD, DIR_ST, DIR_V, E_t, epoch_DP,
       epoch_IS, ex_nop, ext_en, Fl_ECLR, Fl_JPU, Fl_JPU__EP, Fl_MEM, FL_MEM__EP, ft_e, FT_q, halt_FT_DC_ISS,
       halted, hlt, id_full, id_manager_debug_1_eclr_ep, id_manager_debug_1_v, inst_comp_1_a_new,
       inst_comp_2_a_new, inst_comp_4_a_new, inst_comp_5_a_new, inst_comp_6_a_new, inst_comp_7_a_new,
       inst_comp_9_a_new, inst_comp_11_a_new, inst_comp_12_a_new, int_accept, int_epoch, INT_HALT, INT_ISS,
       ISS_B_q, ISS_kernel, ISS_q, issue, issue_e, issue_e__bf, JPU_A__ST, JPU_BTB__J, JPU_BTB__ST,
       JPU_BTB__V, JPU_CALL, JPU_free, JPU_INT, JPU_JP, JPU_LD, JPU_MF, JPU_MFE, JPU_MISS, JPU_RET,
       kernel_inst, LDB_B__MF, LDB_B__RD, LDB_B__ST, LDB_busy, LDB_forward, LDB_ldV, LDB_M__EP, LDB_M__V,
       load_buffer_debug_1_full, load_buffer_debug_1_mf_o, load_buffer_debug_1_v, MB_busy, MB_ep, MB_free,
       MB_LD, MB_ld__e, MB_LDB__LD, MB_MF, MB_MFE, MB_st__e, MB_STB__LD, MB_type__st, MEM_AC, MEM_BF__free,
       MEM_CLR, MEM_EP, MEM_LD, MEM_LD__CLR, MEM_LD__EP, MEM_LD__RD, MEM_LD__REC, MEM_RD, MEM_TYPE__ST, mode,
       monoflop_1_q, monoflop_2_q, multiplexer_8_out, multiplexer_10_out, multiplexer_15_out,
       multiplexer_17_out, multiplexer_20_out, multiplexer_21_out, multiplexer_23_out, multiplexer_24_out,
       multiplexer_25_out, multiplexer_31_out, multiplexer_39_out, multiplexer_40_out, multiplexer_41_out,
       multiplexer_49_out, multiplexer_52_out, multiplexer_54_out, multiplexer_55_out, multiplexer_56_out,
       multiplexer_57_out, multiplexer_59_out, multiplexer_62_out, multiplexer_64_out, multiplexer_65_out,
       multiplexer_73_out, nand_11_out, nand_12_out, nor_1_out, nor_2_out, nor_3_out, nor_4_out, nor_5_out,
       nor_8_out, nor_9_out, nor_11_out, nor_12_out, not_2_out, not_3_out, not_7_out, not_8_out, not_10_out,
       not_11_out, not_12_out, not_13_out, not_14_out, not_15_out, not_17_out, not_18_out, not_20_out,
       not_21_out, not_23_out, not_24_out, not_25_out, not_28_out, not_30_out, not_32_out, not_35_out,
       not_36_out, or_1_out, or_2_out, or_3_out, or_6_out, or_7_out, or_8_out, or_9_out, or_10_out,
       or_19_out, or_21_out, or_22_out, or_27_out, or_29_out, or_30_out, or_31_out, or_32_out, or_35_out,
       or_36_out, or_37_out, or_40_out, or_41_out, or_42_out, or_43_out, or_44_out, or_46_out, or_48_out,
       or_49_out, or_50_out, or_51_out, or_52_out, or_53_out, or_54_out, or_55_out, or_56_out, or_58_out,
       or_59_out, or_60_out, or_61_out, or_65_out, or_66_out, or_69_out, PCA, priorityencoder_1_any,
       register_9_q, register_25_q, register_26_q, register_27_q, register_34_q, register_35_q,
       register_36_q, register_43_q, register_46_q, register_49_q, register_61_q, register_68_q,
       register_71_q, register_74_q, register_79_q, RET_EPOCH, ROB_GEN_DA, ROB_GEN_DB, ROB_GEN_EX1,
       ROB_GEN_EX2, rs_ff_1_nq, rs_ff_3_q, rs_ff_5_nq, rs_ff_5_q, rs_ff_6_q, rs_ff_7_nq, rs_ff_7_q,
       rs_ff_8_nq, rs_ff_9_nq, rs_ff_10_nq, rs_ff_11_nq, rs_ff_12_nq, rs_ff_17_q, rs_ff_18_q, rs_ff_19_q,
       rs_ff_20_q, rs_ff_23_nq, rs_ff_as_1_q, RS_full, run_t, RX_ILVE, RX_ILVM, RX_ISCE, RX_ISCM, RX_PGBSE,
       RX_PGBSM, RX_PVECE, RX_PVECM, STB_busy, STB_M__EP, STB_M__V, store_buffer_debug_1_full, sub_1_c_o,
       TRAP_busy, TRAP_free, TRAP_IRD, TRAP_RD, TRAP_ST, V_q, \wait , waiting, xor_2_out;
  wire [0:0] and_97_out, JPU_BTBPK, keyboard_1_av;
  wire [1:0] and_110_out, and_112_out, and_127_out, and_128_out, bitextender_6_out, bitextender_7_out,
       d_ff_5_q, d_ff_9_q, d_ff_10_q, d_ff_11_q, d_ff_12_q, JPU_BTB__pred, JPU_pred, LDB_M__MD, MB_MD,
       multiplexer_13_out, or_23_out, register_17_q, STB_M__MD, store_controller_half_1_d1_sel,
       store_controller_half_1_d2_sel, store_controller_half_2_d1_sel, store_controller_half_2_d2_sel;
  wire [1:1] or_20_out, register_47_q, register_72_q;
  wire [2:0] ALU_A_RM, ALU_B_RM, and_100_out, and_104_out, CT_ISS__UFU, CT_RF__MA, CT_RF__MB, CT_RF__SCN,
       CT_RF__WM, CT_SP__MOF, multiplexer_18_out, multiplexer_47_out, nand_1_out, nand_2_out, nand_4_out,
       nand_8_out, not_19_out, not_22_out, register_23_q, register_48_q, store_controller_1_d1_sel,
       store_controller_1_d2_sel;
  wire [2:1] nor_6_out;
  wire [3:0] ALU_A_INST, ALU_B_INST, clr_id, clrs_id, com1_inst, com2_inst, CT_FU__INST, DIR_INST,
       Fl_JPU__INST, FL_MEM__ID, FU_I__V, id_manager_debug_1_eclr_id, inst_DP, inst_IS, int_inst, LD_id,
       LDB_B__INST, LDB_M__ID, load_buffer_debug_1_id_o, MB_INST, MEM_INST, MEM_LD__INST, multiplexer_6_out,
       multiplexer_22_out, multiplexer_38_out, multiplexer_48_out, multiplexer_58_out, multiplexer_67_out,
       multiplexer_72_out, priorityencoder_1_num, register_24_q, register_33_q, register_42_q, register_67_q,
       RET_INST, ROB_FL_INSTA, ROB_FL_INSTB, ROB_GEN_INSTA, ROB_GEN_INSTB, ROB_INT_INSTA, ROB_INT_INSTB,
       STB_M__ID, TRAP_INST;
  wire [3:2] FU_F__V;
  wire [4:0] CT_ISS__RA, CT_ISS__RB, CT_ISS__RC, CT_RF__RA, CT_RF__RB, CT_RF__WS;
  wire [4:4] FU_CLR;
  wire [5:0] CT_INT__D, ROB_INT_A, ROB_INT_B, TRAP_INT;
  wire [6:6] and_197_out;
  wire [7:0] ALU_A_F, ALU_A_FI, ALU_A_T__F, ALU_B_F, ALU_B_FI, ALU_B_T__F, bitextender_3_out, byte_D0,
       byte_D0_iv, byte_D1, byte_D2, byte_D3, byte_I0, byte_I0_iv, byte_I1, byte_I2, byte_I3, counter_3_out,
       CT_DIR__EXID, CT_FL__D1, CT_FL__D2, CT_FU__WR, CT_INTID, CT_RF__R1, CT_RF__R2, demultiplexer_1_out_0,
       demultiplexer_2_out_0, DIR_WR, fl_i, FU_free, LDB_B__WR, load_buffer_debug_1_wr_o, MB_WR,
       multiplexer_9_out, multiplexer_28_out, multiplexer_30_out, multiplexer_44_out, multiplexer_46_out,
       multiplexer_51_out, multiplexer_61_out, or_4_out, register_30_q, register_32_q, register_39_q,
       register_41_q, register_45_q, register_70_q, ROB_FL_A, ROB_FL_B, ROB_GEN_WA, ROB_GEN_WB, xor_3_out;
  wire [7:3] ALU_A_WR, ALU_B_WR, FU_D__V;
  wire [7:6] register_11_q;
  wire [8:0] ALU_A_CT, ALU_B_CT, CT_ALU__CT, multiplexer_29_out, multiplexer_45_out, register_31_q,
       register_40_q;
  wire [9:0] and_42_out;
  wire [15:0] and_178_out, and_180_out, and_182_out, and_183_out, and_185_out, bitextender_4_out,
       bitextender_5_out, bitextender_8_out, bitextender_10_out, bitextender_11_out, clr_16, clrs_16,
       d_ff_21_q, demultiplexer_3_out_0, demultiplexer_4_out_0, E_inst, icmk_16, icmks_16,
       id_manager_debug_1_c16, id_manager_debug_1_us, id_manager_debug_1_vv1, id_manager_debug_1_vv2,
       keyboard_1_d, multiplexer_36_out, multiplexer_76_out, not_33_out, not_34_out, or_62_out, or_63_out,
       or_64_out, register_55_q, register_93_q, register_97_q, register_98_q, V1_inst, V2_inst;
  wire [16:0] rom_1_d;
  wire [31:0] A_q, add_1_s, add_4c32_1_s, add_4c32_2_s, add_4c32_3_s, addsub_4c32_1_s, alu_32_1_p8,
       alu_32_1_p11, alu_32_1_p12, alu_32_1_p14, ALU_A_A, ALU_A_B, ALU_A_R, ALU_A_T__R, ALU_B_A, ALU_B_B,
       ALU_B_R, ALU_B_T__R, bitextender_1_out, bitextender_2_out, counter_1_out, counter_2_out, CT_RF__D1,
       CT_RF__D2, CT_RF__DR, CT_SC__D1, CT_SC__D2, CT_SC__FD, d_ff_20_q, D_q, DIR, FL, HALT_PC, I_A__R_q,
       I_D__R_q, int_pc, int_vec_t, ISC, ISC_i, ISC_sc, JPU_ADDR, JPU_BTB__tar, JPU_PC, LD_addr, LDB_B__D,
       LDB_ldD, LDB_M__A, MB_addr, MB_data, MB_PC, MEM_FPC, MEM_LD__D, multiplexer_2_out, multiplexer_5_out,
       multiplexer_7_out, multiplexer_11_out, multiplexer_12_out, multiplexer_16_out, multiplexer_19_out,
       multiplexer_26_out, multiplexer_27_out, multiplexer_32_out, multiplexer_33_out, multiplexer_34_out,
       multiplexer_35_out, multiplexer_37_out, multiplexer_42_out, multiplexer_43_out, multiplexer_50_out,
       multiplexer_60_out, multiplexer_66_out, multiplexer_69_out, multiplexer_71_out, multiplexer_74_out,
       multiplexer_75_out, mVec, pc_read, pc_ret__int, pca_i, PCS, PCS_DC, PCS_FT, pcs_i, PVEC, PVEC_i, R_A,
       R_B, ramdualaccess_1_d1, ramdualaccess_1_d2, register_5_q, register_12_q, register_16_q,
       register_18_q, register_28_q, register_29_q, register_37_q, register_38_q, register_44_q,
       register_54_q, register_69_q, register_92_q, RX_SEL, SCA, sca_i, SCS, STB_M__A, STB_M__D;
  wire [31:24] res_station_debug_1_disp_32;
  wire [36:0] and_179_out, bitextender_9_out, BTB_D_q, BTB_DP, BTB_fetch, BTB_pack__iss, BTB_packet;

  Comparator #(.Bits(32)) comparator_1 (.a(PCS), .b(32'h40), .eq(comparator_1_eq));  // open: gt, lt
  Comparator #(.Bits(32)) comparator_2 (.a(PCS), .b(32'h58), .eq(comparator_2_eq));  // open: gt, lt
  RS_FF_AS rs_ff_as_1 (.S(run_t), .R(dipswitch_1_out), .Q(rs_ff_as_1_q));  // open: nQ
  DipSwitch dipswitch_1 (.out(dipswitch_1_out));
  LED led_1 (.in(comparator_1_eq));
  LED led_2 (.in(comparator_2_eq));
  DipSwitch #(.dipDefault("true")) dipswitch_2 (.out(dipswitch_2_out));
  DipSwitch dipswitch_3 (.out(dipswitch_3_out));
  // Probe E on E_t
  // Probe R on run_t
  // Probe issue_e on issue_e
  // Probe CT_ISS-_OLDB on CT_ISS__OLDB
  // Probe clr on clr
  // Probe halt-FT-DC-ISS on halt_FT_DC_ISS
  // Probe issue_32 on {byte_I0, byte_I1, byte_I2, byte_I3}
  // Probe disp_32 on {byte_D0, byte_D1, byte_D2, byte_D3}
  // Probe FL_MEM on Fl_MEM
  // Probe FL_JPU on Fl_JPU
  // Probe FL_ECLR on Fl_ECLR
  // Probe FL_INT on INT_out
  // Probe on com1
  // Probe on com2
  // Probe on com1_inst
  // Probe on com2_inst
  // Probe on epoch_IS
  // Probe on inst_IS
  Comparator #(.Bits(32)) comparator_3 (.a(counter_1_out), .b(32'h50), .gt(comparator_3_gt));  // open: eq, lt
  Comparator #(.Bits(32)) comparator_4 (.a(counter_1_out), .b(32'hc), .eq(comparator_4_eq));  // open: gt, lt
  Comparator #(.Bits(32)) comparator_5 (.a(counter_1_out), .b(32'h14), .eq(comparator_5_eq));  // open: gt, lt
  Comparator #(.Bits(32)) comparator_6 (.a(counter_1_out), .b(32'h16), .eq(comparator_6_eq));  // open: gt, lt
  Counter #(.Bits(32)) counter_1 (
    .en(dipswitch_2_out), .C(C_dt), .clr(dipswitch_3_out), .out(counter_1_out));  // open: ovf
  Counter #(.Bits(32)) counter_2 (
    .en(rs_ff_as_1_q), .C(C_dt), .clr(dipswitch_1_out), .out(counter_2_out));  // open: ovf
  // Probe cycle on counter_1_out
  // Probe Ecycle on counter_2_out
  PullDown #(.Bits(32)) pulldown_1 (.out(I_A__bus));
  RS_FF_AS rs_ff_as_2 (.S(comparator_4_eq), .R(dipswitch_4_out), .Q(E_t));  // open: nQ
  DipSwitch dipswitch_4 (.out(dipswitch_4_out));
  RS_FF_AS rs_ff_as_3 (.S(comparator_5_eq), .R(comparator_6_eq), .Q(run_t));  // open: nQ
  LED led_3 (.in(MB_ld__e));
  LED led_4 (.in(MB_st__e));
  DipSwitch dipswitch_5 (.out(dipswitch_5_out));
  DipSwitch dipswitch_6 (.out(dipswitch_6_out));
  Multiplexer multiplexer_1 (.sel(dipswitch_5_out), .in_0(dipswitch_6_out), .in_1(C), .out(C_dt));
  not not_1 (C_ct, C_dt);
  not not_2 (not_2_out, I_valid);
  assign CT_BUS__IDM = not_2_out ? 1'b1 : 1'bz;  // Driver driver_1
  and and_1 (and_1_out, I_valid, ft_e);
  assign CT_RF__PCSE = and_1_out ? 1'b1 : 1'bz;  // Driver driver_2
  assign CT_BUS__IAR = and_1_out ? 1'b1 : 1'bz;  // Driver driver_3
  assign CT_BUS__IAG = ft_e ? 1'b1 : 1'bz;  // Driver driver_4
  assign I_LD = ft_e ? 1'b1 : 1'bz;  // Driver driver_5
  or or_1 (or_1_out, issue, INT_ISS);
  not not_3 (not_3_out, clr_sel);
  Comparator #(.Bits(32)) comparator_7 (.a(PCS), .b(mVec), .gt(comparator_7_gt));  // open: eq, lt
  BitExtender #(.inputBits(16), .outputBits(32)) bitextender_1 (.in({byte_D2, byte_D3}), .out(bitextender_1_out));
  RS_FF rs_ff_1 (.S(INT_out), .C(C_ct), .R(CT_INTM), .nQ(rs_ff_1_nq));  // open: Q
  and and_2 (INT_out, rs_ff_1_nq, int_accept);
  PullDown pulldown_2 (.out(CT_ISCSM));
  PullDown pulldown_3 (.out(CT_ISCCM));
  PullDown pulldown_4 (.out(CT_ISCE));
  PullDown pulldown_5 (.out(JPU_INT));
  and and_3 (and_3_out, INT_nor, ~halted);  // And
  and and_4 (and_4_out, waiting, INT_nor, ~halted);  // And
  Register #(.Bits(32)) u_ISC (.D(ISC_i), .C(C_dt), .en(CT_ISCE), .Q(ISC));
  Register #(.Bits(32)) register_1 (.D(INT_vec), .C(C_dt), .en(int_accept), .Q(int_vec_t));
  and and_5 (and_5_out, nor_1_out, CT_RF__W1, CT_RF__EX1);
  PullDown #(.Bits(32)) pulldown_6 (.out(D_A__bus));
  LED led_5 (.in(CT_JPU__LD));
  LED led_6 (.in(D_ST));
  LED led_7 (.in(JPU_BTB__ST));
  LED led_8 (.in(Fl_MEM));
  LED led_9 (.in(epoch_IS));
  // Probe ID on inst_DP
  id_manager_debug id_manager_debug_1 (
    .C(C_ct), .\use (or_1_out), .S1_inst(V1_inst), .S2_inst(V2_inst), .E_inst(E_inst), .clr(clr),
    .clr_self(not_3_out), .clr_ep(clr_ep), .clr_id(clr_id), .epoch(epoch_IS), .id(inst_IS),
    .V(id_manager_debug_1_v), .com1(com1), .com1_id(com1_inst), .com1_ep(com1_ep), .com2(com2),
    .com2_id(com2_inst), .com2_ep(com2_ep), .ext_en(ext_en), .cmk_16(icmk_16), .clr_16(clr_16),
    .cmks_16(icmks_16), .clrs_16(clrs_16), .VV1(id_manager_debug_1_vv1), .VV2(id_manager_debug_1_vv2),
    .US(id_manager_debug_1_us), .C16(id_manager_debug_1_c16), .eclr_v(Fl_ECLR),
    .eclr_id(id_manager_debug_1_eclr_id), .eclr_ep(id_manager_debug_1_eclr_ep));
  flush_mux flush_mux_1 (
    .M_v(Fl_MEM), .M_id(FL_MEM__ID), .M_ep(FL_MEM__EP), .J_v(Fl_JPU), .J_id(Fl_JPU__INST), .J_ep(Fl_JPU__EP),
    .I_v(INT_out), .I_id(com2_inst), .I_ep(com2_ep), .sel(clr_sel), .m_v_2(clr), .m_id_2(clr_id),
    .m_ep_2(clr_ep), .E_v(Fl_ECLR), .E_id(id_manager_debug_1_eclr_id), .E_ep(id_manager_debug_1_eclr_ep));
  Add #(.Bits(32)) add_1 (.a(R_A), .b(bitextender_1_out), .c_i(1'b0), .s(add_1_s));  // open: c_o
  Demultiplexer #(.Selector_Bits(3)) demultiplexer_1 (
    .sel(CT_RF__R1[2:0]), .in(and_5_out), .out_0(demultiplexer_1_out_0[0]), .out_1(demultiplexer_1_out_0[1]),
    .out_2(demultiplexer_1_out_0[2]), .out_3(demultiplexer_1_out_0[3]), .out_4(demultiplexer_1_out_0[4]),
    .out_5(demultiplexer_1_out_0[5]), .out_6(demultiplexer_1_out_0[6]), .out_7(demultiplexer_1_out_0[7]));
  Comparator #(.Bits(6)) comparator_8 (.a(D_A__bus[31:26]), .b({6{1'b0}}), .eq(comparator_8_eq));  // open: gt, lt
  Comparator #(.Bits(6)) comparator_9 (.a(I_A__bus[31:26]), .b({6{1'b0}}), .eq(comparator_9_eq));  // open: gt, lt
  // Probe on CT_RF__WS
  // Probe on CT_RF__WM
  // Probe on CT_RF__RA
  // Probe on CT_RF__MA
  // Probe on CT_RF__RB
  // Probe on CT_RF__MB
  and and_6 (and_6_out, 1'b0, ~comparator_7_gt);  // And
  D_FF d_ff_1 (.D(INT_out), .C(C_ct), .Q(d_ff_1_q));  // open: nQ
  Multiplexer #(.Bits(32)) multiplexer_2 (.sel(RX_ISCM), .in_0(CT_RF__D1), .in_1(CT_RF__D2), .out(multiplexer_2_out));
  or or_2 (or_2_out, and_3_out, and_4_out);
  nor nor_1 (nor_1_out, CT_RF__R1[7], CT_RF__R1[6], CT_RF__R1[5], CT_RF__R1[4], CT_RF__R1[3]);
  Comparator #(.Bits(6)) comparator_10 (.a(D_A__bus[31:26]), .b(6'b000010), .eq(comparator_10_eq));  // open: gt, lt
  and and_7 (and_7_out, comparator_8_eq, D_LD);
  and and_8 (and_8_out, D_ST, comparator_8_eq);
  and and_9 (and_9_out, comparator_9_eq, I_LD);
  Comparator #(.Bits(30)) comparator_11 (.a(D_A__bus[31:2]), .b(30'h1000000), .eq(comparator_11_eq));  // open: gt, lt
  Comparator #(.Bits(30)) comparator_12 (.a(D_A__bus[31:2]), .b(30'h1000001), .eq(comparator_12_eq));  // open: gt, lt
  Comparator #(.Bits(30)) comparator_13 (.a(D_A__bus[31:2]), .b(30'h1000002), .eq(comparator_13_eq));  // open: gt, lt
  Comparator #(.Bits(30)) comparator_14 (.a(D_A__bus[31:2]), .b(30'h1000003), .eq(comparator_14_eq));  // open: gt, lt
  DipSwitch dipswitch_7 (.out(dipswitch_7_out));
  DipSwitch dipswitch_8 (.out(dipswitch_8_out));
  LED led_10 (.in(halt_FT_DC_ISS));
  LED led_11 (.in(clr));
  LED led_12 (.in(LDB_B__RD));
  // Probe FU on FU_free
  // Probe INST on {byte_I0, byte_I1, byte_I2, byte_I3}
  // Probe INST on {byte_D0, byte_D1, byte_D2, byte_D3}
  or or_3 (or_3_out, run_t, INT_out);
  not not_4 (id_full, id_manager_debug_1_v);
  RS_FF u_mode (.S(and_6_out), .C(C_dt), .R(comparator_7_gt), .Q(mode));  // open: nQ
  Register #(.Bits(32)) MVR (.D(add_1_s), .C(C_dt), .en(CT_MVR), .Q(mVec));
  RS_FF rs_ff_2 (.S(INT_out), .C(C_ct), .R(INT_ISS), .Q(INT_HALT));  // open: nQ
  RS_FF rs_ff_3 (.S(d_ff_1_q), .C(C_ct), .R(INT_ISS), .Q(rs_ff_3_q));  // open: nQ
  Comparator #(.Bits(4)) comparator_15 (.a(inst_IS), .b(com1_inst), .eq(comparator_15_eq));  // open: gt, lt
  assign CT_JPU__LD = INT_ISS ? 1'b1 : 1'bz;  // Driver driver_6
  assign JPU_INT = INT_ISS ? 1'b1 : 1'bz;  // Driver driver_7
  assign CT_ISS__OSTB = INT_ISS ? 1'b1 : 1'bz;  // Driver driver_8
  Register #(.Bits(32)) register_2 (.D(PCS_DC), .C(C_dt), .en(INT_ISS), .Q(int_pc));
  Register #(.Bits(4)) register_3 (.D(inst_IS), .C(C_ct), .en(INT_ISS), .Q(int_inst));
  Register register_4 (.D(epoch_IS), .C(C_ct), .en(INT_ISS), .Q(int_epoch));
  assign {or_4_out[7:5], RX_PGBSE, RX_ILVE, RX_ISCE, RX_PVECE, or_4_out[0]} = {demultiplexer_2_out_0[7:5], RX_PGBSM, RX_ILVM, RX_ISCM, RX_PVECM, demultiplexer_2_out_0[0]} | demultiplexer_1_out_0;  // Or or_4, 8 bits wide
  and and_10 (and_10_out, comparator_10_eq, D_LD);
  and and_11 (and_11_out, D_ST, comparator_10_eq);
  and and_12 (and_12_out, D_LD, comparator_11_eq);
  and and_13 (and_13_out, D_LD, comparator_12_eq);
  and and_14 (and_14_out, D_ST, C_dt, comparator_13_eq);
  and and_15 (and_15_out, D_ST, comparator_14_eq);
  LED led_13 (.in(LDB_B__ST));
  LED led_14 (.in(JPU_CALL));
  and and_16 (and_16_out, JPU_CALL, dipswitch_7_out);
  LED led_15 (.in(CT_RET__LD));
  and and_17 (and_17_out, CT_RET__LD, dipswitch_8_out);
  LED led_16 (.in(LDB_forward));
  assign byte_I0_iv = ~byte_I0;  // Not not_5, 8 bits wide
  assign byte_D0_iv = ~byte_D0;  // Not not_6, 8 bits wide
  nor nor_2 (nor_2_out, clr, \wait );
  Multiplexer #(.Bits(32)) multiplexer_3 (.sel(CT_ISCSM), .in_0(multiplexer_2_out), .in_1(ISC_sc), .out(ISC_i));
  assign CT_ISCE = RX_ISCE ? 1'b1 : 1'bz;  // Driver driver_9
  and and_18 (and_18_out, nor_3_out, CT_RF__W2, CT_RF__EX2);
  DipSwitch dipswitch_9 (.out(dipswitch_9_out));
  RAMDualAccess #(.AddrBits(24), .isProgramMemory("true"), .Bits(32)) ramdualaccess_1 (
    .str(and_8_out), .C(C_dt), .ld(1'b1), .A1(D_A__bus[25:2]), .Din1(D_D__bus), .A2(I_A__bus[25:2]),
    .D1(ramdualaccess_1_d1), .D2(ramdualaccess_1_d2));
  Counter #(.Bits(8)) counter_3 (.en(1'b1), .C(and_14_out), .clr(1'b0), .out(counter_3_out));  // open: ovf
  // Probe inst on {byte_I0, byte_I1, byte_I2, byte_I3}
  // Probe R_A on R_A
  // Probe R_B on R_B
  // Probe PC on PCS
  // Probe SCS on SCS
  // Probe SCA on SCA
  // Probe FL on FL
  // Probe CT_BUS-_IDM on CT_BUS__IDM
  // Probe C_i on C_dt
  Monoflop monoflop_1 (.C(and_16_out), .R(dipswitch_10_out), .Q(monoflop_1_q));  // open: nQ
  DipSwitch dipswitch_10 (.out(dipswitch_10_out));
  Monoflop monoflop_2 (.C(and_17_out), .R(dipswitch_11_out), .Q(monoflop_2_q));  // open: nQ
  DipSwitch dipswitch_11 (.out(dipswitch_11_out));
  Register #(.Bits(32)) D (.D(D_D__bus), .C(C_dt), .en(D_ST), .Q(D_q));
  Register #(.Bits(32)) A (.D(D_A__bus), .C(C_dt), .en(D_ST), .Q(A_q));
  RS_FF FT (.S(or_3_out), .C(C_ct), .R(\wait ), .Q(FT_q), .nQ(waiting));
  not not_7 (not_7_out, halt_FT_DC_ISS);
  and and_19 (INT_ISS, rs_ff_3_q, comparator_15_eq, ~STB_busy);  // And
  D_FF d_ff_2 (.D(INT_nor), .C(C_dt), .Q(d_ff_2_q));  // open: nQ
  nor nor_3 (nor_3_out, CT_RF__R2[7], CT_RF__R2[6], CT_RF__R2[5], CT_RF__R2[4], CT_RF__R2[3]);
  Demultiplexer #(.Selector_Bits(3)) demultiplexer_2 (
    .sel(CT_RF__R2[2:0]), .in(and_18_out), .out_0(demultiplexer_2_out_0[0]), .out_1(RX_PVECM),
    .out_2(RX_ISCM), .out_3(RX_ILVM), .out_4(RX_PGBSM), .out_5(demultiplexer_2_out_0[5]),
    .out_6(demultiplexer_2_out_0[6]), .out_7(demultiplexer_2_out_0[7]));
  GraphicCard #(.graphicHeight(90), .Bits(32)) graphiccard_1 (
    .A(D_A__bus[16:2]), .str(and_11_out), .C(C_dt), .ld(and_10_out), .B(dipswitch_9_out), .D(D_D__bus));
  assign D_D__bus = and_7_out ? ramdualaccess_1_d1 : 32'bz;  // Driver driver_10
  assign I_D__bus = and_9_out ? ramdualaccess_1_d2 : 32'bz;  // Driver driver_11
  ROM #(.AddrBits(8), .Bits(17)) rom_1 (.A(counter_3_out), .sel(1'b1), .D(rom_1_d));
  Keyboard keyboard_1 (.C(and_14_out), .en(1'b1), .D(keyboard_1_d), .av(keyboard_1_av[0]));
  Terminal terminal_1 (.D(D_D__bus), .C(C_dt), .en(and_15_out));
  and and_20 (and_20_out, byte_D0_iv[0], byte_D0[1], byte_D0[2], byte_D0_iv[3], byte_D0[4], byte_D0[5], byte_D0[6], byte_D0_iv[7]);
  Break #(.Cycles(1000000)) A_2 (.brk(monoflop_1_q));
  Break #(.Cycles(1000000)) A_3 (.brk(monoflop_2_q));
  // Probe on D_q
  // Probe on A_q
  and and_21 (and_21_out, nor_2_out, FT_q);
  // Probe V1_inst on V1_inst
  // Probe VG1_inst on id_manager_debug_1_vv1
  // Probe V2_inst on V2_inst
  // Probe VG2_inst on id_manager_debug_1_vv2
  // Probe U_inst on id_manager_debug_1_us
  // Probe CLR_inst on id_manager_debug_1_c16
  D_FF d_ff_3 (.D(INT_ISS), .C(C_ct), .Q(CT_INTM));  // open: nQ
  D_FF d_ff_4 (.D(d_ff_2_q), .C(C_ct), .Q(int_accept));  // open: nQ
  Register #(.Bits(32)) register_5 (.D(D_D__bus), .C(C_dt), .en(and_11_out), .Q(register_5_q));
  and and_22 (and_22_out, comparator_3_gt, ~rom_1_d[16]);  // And
  and and_23 (and_23_out, nor_2_out, FT_q);
  Register DC (.D(and_23_out), .C(C_ct), .en(1'b1), .Q(DC_q));
  and and_24 (ft_e, FT_q, not_7_out);
  Register DC_B (.D(and_21_out), .C(C_dt), .en(1'b1), .Q(DC_B_q));
  Register #(.Bits(32)) register_6 (.D(PCS), .C(C_dt), .en(CT_RF__PCSE), .Q(PCS_FT));
  // Probe on register_5_q
  assign D_D__bus = and_12_out ? {{16{1'b0}}, keyboard_1_d} : 32'bz;  // Driver driver_12
  assign D_D__bus = and_13_out ? {{31{1'b0}}, keyboard_1_av[0]} : 32'bz;  // Driver driver_13
  // Probe com1 on com1
  // Probe com2 on com2
  // Probe com1_inst on com1_inst
  // Probe com2_inst on com2_inst
  // Probe PC_inst on inst_IS
  and and_25 (and_25_out, nor_2_out, DC_B_q);
  and and_26 (and_26_out, DC_B_q, not_7_out);
  DipSwitch dipswitch_12 (.out(dipswitch_12_out));
  Sub #(.Bits(4)) sub_1 (.a(clr_id), .b(4'b0000), .c_i(not_8_out), .s(clrs_id), .c_o(sub_1_c_o));
  not not_8 (not_8_out, clr_sel);
  assign MB_LD = CT_INTM ? 1'b1 : 1'bz;  // Driver driver_14
  assign CT_MB__ST = CT_INTM ? 1'b1 : 1'bz;  // Driver driver_15
  assign CT_FU__INST = CT_INTM ? int_inst : 4'bz;  // Driver driver_16
  assign CT_FU__EPOCH = CT_INTM ? int_epoch : 1'bz;  // Driver driver_17
  assign CT_ISCCM = CT_INTM ? 1'b1 : 1'bz;  // Driver driver_18
  assign CT_ISCE = CT_INTM ? 1'b1 : 1'bz;  // Driver driver_19
  assign CT_RF__SCD = CT_INTM ? 1'b1 : 1'bz;  // Driver driver_20
  assign CT_RF__SCN = CT_INTM ? 3'b100 : 3'bz;  // Driver driver_21
  assign CT_ISCSM = CT_INTM ? 1'b1 : 1'bz;  // Driver driver_22
  Multiplexer #(.Bits(32)) multiplexer_4 (.sel(RX_PVECM), .in_0(CT_RF__D1), .in_1(CT_RF__D2), .out(PVEC_i));
  assign CT_PVECE = RX_PVECE ? 1'b1 : 1'bz;  // Driver driver_23
  PullDown pulldown_7 (.out(CT_PVECE));
  Register #(.Bits(32)) u_PVEC (.D(PVEC_i), .C(C_dt), .en(CT_PVECE), .Q(PVEC));
  Multiplexer #(.Selector_Bits(3), .Bits(32)) multiplexer_5 (
    .sel(CT_DIR__EXID[2:0]), .in_0(32'h1), .in_1(PVEC), .in_2(ISC), .in_3({32{1'b0}}), .in_4({32{1'b0}}),
    .in_5({32{1'b0}}), .in_6({32{1'b0}}), .in_7({32{1'b0}}), .out(multiplexer_5_out));
  assign CT_FU__EPOCH = and_20_out ? epoch_DP : 1'bz;  // Driver driver_24
  assign CT_FU__INST = and_20_out ? inst_DP : 4'bz;  // Driver driver_25
  assign CT_TRAP__LD = and_20_out ? 1'b1 : 1'bz;  // Driver driver_26
  and and_27 (and_27_out, nor_2_out, DC_q);
  Register ISS (.D(and_27_out), .C(C_ct), .en(1'b1), .Q(ISS_q));
  and and_28 (dc_e, DC_q, not_7_out);
  Register ISS_B (.D(and_25_out), .C(C_dt), .en(1'b1), .Q(ISS_B_q));
  Register #(.Bits(32)) register_7 (.D(PCS_FT), .C(C_dt), .en(CT_RF__PCSE), .Q(PCS_DC));
  or or_5 (halt_FT_DC_ISS, id_full, RS_full, INT_HALT, dipswitch_13_out, dipswitch_12_out, LDB_busy, STB_busy);
  DipSwitch dipswitch_13 (.out(dipswitch_13_out));
  xor xor_1 (clrs_ep, clr_ep, sub_1_c_o);
  nor nor_4 (nor_4_out, CT_DIR__EXID[7], CT_DIR__EXID[6], CT_DIR__EXID[5], CT_DIR__EXID[4], CT_DIR__EXID[3]);
  assign RX_SEL = bitextender_2_out & multiplexer_5_out;  // And and_29, 32 bits wide
  and and_30 (issue_e__bf, ISS_B_q, not_7_out);
  PullDown pulldown_8 (.out(CT_DISP));
  PullDown pulldown_9 (.out(CT_rollback));
  PullDown pulldown_10 (.out(com2));
  PullDown #(.Bits(4)) pulldown_11 (.out(com2_inst));
  PullDown pulldown_12 (.out(com1_M));
  PullDown pulldown_13 (.out(com1));
  PullDown #(.Bits(4)) pulldown_14 (.out(com1_inst));
  BitExtender #(.inputBits(1), .outputBits(32)) bitextender_2 (.in(nor_4_out), .out(bitextender_2_out));
  and and_31 (issue_e, ISS_q, not_7_out);
  Multiplexer #(.Bits(4)) multiplexer_6 (.sel(com2), .in_0(com1_inst), .in_1(com2_inst), .out(multiplexer_6_out));
  ROB_SC rob_sc_1 (
    .C(C_dt), .E(CT_RF__SCSRE), .D(ISC_sc), .inst(inst_DP), .com1(com1), .com2(com2), .com1_id(com1_inst),
    .com2_id(com2_inst), .clr_16(clr_16), .roll(clr_id), .SCA(SCA), .W1(CT_SC__W1), .D1(CT_SC__D1),
    .W2(CT_SC__W2), .D2(CT_SC__D2), .D3(CT_SC__FD));
  BTB btb_1 (
    .C(C_dt), .E(JPU_BTB__ST), .V_in(1'b1), .id(JPU_PC[5:2]), .tag(JPU_PC[17:6]), .pred(JPU_pred),
    .tar(JPU_ADDR), .R_id(PCS[5:2]), .R_tag(PCS[17:6]), .V(BTB_packet[1]), .J(BTB_JP),
    .pred_O(BTB_packet[4:3]), .tar_O(BTB_packet[36:5]));
  or or_6 (or_6_out, MEM_AC, MEM_CLR);
  not not_9 (MEM_LD__REC, LDB_forward);
  inst_comp inst_comp_1 (.A_id(MEM_INST), .A_ep(MEM_EP), .B_id(clrs_id), .B_ep(clrs_ep), .A_new(inst_comp_1_a_new));
  inst_comp inst_comp_2 (
    .A_id(MEM_LD__INST), .A_ep(MEM_LD__EP), .B_id(clrs_id), .B_ep(clrs_ep), .A_new(inst_comp_2_a_new));
  Comparator #(.Bits(4)) comparator_16 (.a(TRAP_INST), .b(com1_inst), .eq(comparator_16_eq));  // open: gt, lt
  Comparator #(.Bits(4)) comparator_17 (.a(TRAP_INST), .b(com2_inst), .eq(comparator_17_eq));  // open: gt, lt
  Register #(.Bits(4)) register_8 (.D(CT_FU__INST), .C(C_ct), .en(CT_TRAP__LD), .Q(TRAP_INST));
  Register register_9 (.D(CT_FU__EPOCH), .C(C_ct), .en(CT_TRAP__LD), .Q(register_9_q));
  Register register_10 (.D(CT_INT), .C(C_ct), .en(CT_TRAP__LD), .Q(TRAP_IRD));
  Register #(.Bits(8)) register_11 (.D(CT_INTID), .C(C_ct), .en(CT_TRAP__LD), .Q({register_11_q, TRAP_INT}));
  RS_FF rs_ff_4 (.S(CT_TRAP__LD), .C(C_ct), .R(FU_CLR[4]), .Q(TRAP_RD));  // open: nQ
  D_FF #(.Bits(2)) d_ff_5 (.D({LDB_M__V, STB_M__V}), .C(C_ct), .Q(d_ff_5_q));  // open: nQ
  and and_32 (and_32_out, ~MEM_LD, or_6_out);  // And
  and and_33 (and_33_out, com1, comparator_16_eq);
  and and_34 (and_34_out, com2, comparator_17_eq);
  // ROB_gen rob_gen_1: pin names not known; wires that end beside it: C_dt, CT_ROB__GEN__STA, CT_ROB__GEN__STB, ROB_GEN_DA, ROB_GEN_DB, ROB_GEN_WA, ROB_GEN_WB, ROB_GEN_EX1, ROB_GEN_EX2, ROB_GEN_INSTA, ROB_GEN_INSTB, com1, com2, com1_inst, com2_inst, clr_16, RET_INST, CT_RF__D1, CT_RF__R1, CT_RF__W1, CT_RF__EX1, CT_RF__D2, CT_RF__R2, CT_RF__W2, CT_RF__EX2, CT_RF__DR
  ROB_PC rob_pc_1 (
    .C(C_dt), .E(issue), .D(PCS_DC), .inst(inst_IS), .com_id(multiplexer_6_out), .read_id(inst_DP),
    .ret_id(RET_INST), .D1(pca_i), .D2(pc_read), .D3(pc_ret__int));
  DipSwitch dipswitch_14 (.out(BTB_packet[0]));
  or or_7 (or_7_out, multiplexer_10_out, MEM_BF__free);
  or or_8 (or_8_out, d_ff_5_q[0], d_ff_5_q[1], MEM_CLR);
  RS_FF rs_ff_5 (.S(MEM_LD), .C(C_ct), .R(and_32_out), .Q(rs_ff_5_q), .nQ(rs_ff_5_nq));
  and and_35 (MEM_CLR, inst_comp_1_a_new, ~MEM_TYPE__ST, clr);  // And
  and and_36 (MEM_LD__CLR, inst_comp_2_a_new, clr);
  or or_9 (or_9_out, and_33_out, and_34_out);
  inst_comp inst_comp_3 (.A_id(TRAP_INST), .A_ep(register_9_q), .B_id(clr_id), .B_ep(clr_ep), .A_new(FU_CLR[4]));
  bus16x2_demux bus16x2_demux_1 (.bus_1(V1_inst), .bus_2(V2_inst), .E(FU_I__V[0]), .id(TRAP_INST));
  and and_37 (and_37_out, byte_D0[3], byte_D0[0]);
  and and_38 (and_38_out, byte_D0[2], byte_D0[0]);
  and and_39 (and_39_out, byte_D0_iv[3], byte_D0_iv[2], byte_D0[1], byte_D0_iv[0]);
  and and_40 (and_40_out, byte_D0_iv[4], byte_D0[3], byte_D0[2], byte_D0[1]);
  and and_41 (and_41_out, byte_D0[4], byte_D0_iv[3], byte_D0_iv[2], byte_D0[1], byte_D0[0]);
  and and_42 (and_42_out[7], byte_D0_iv[4], byte_D0[3], byte_D0[2]);
  and and_43 (and_43_out, byte_D0[4], byte_D0[2], byte_D0_iv[1]);
  and and_44 (and_44_out, byte_D0[4], byte_D0_iv[3], byte_D0_iv[2]);
  and and_45 (and_45_out, byte_D0_iv[4], byte_D0_iv[3], byte_D0_iv[2]);
  and and_46 (and_46_out, byte_D0_iv[4], byte_D0_iv[3]);
  and and_47 (and_47_out, byte_D0_iv[4], byte_D0[3], byte_D0_iv[2], byte_D0_iv[1]);
  and and_48 (and_48_out, byte_D0_iv[4], byte_D0[3], byte_D0_iv[2]);
  and and_49 (and_49_out, byte_D0[4], byte_D0[3]);
  and and_50 (and_50_out, byte_D0_iv[4], byte_D0_iv[3], byte_D0[2], byte_D0_iv[1]);
  and and_51 (and_51_out, byte_D0[4], byte_D0[2], byte_D0[1]);
  and and_52 (and_52_out, byte_D0_iv[4], byte_D0_iv[3], byte_D0_iv[2], byte_D0[1], byte_D0[0]);
  and and_53 (and_53_out, byte_D0_iv[2], byte_D0_iv[0]);
  and and_54 (and_54_out, byte_D0[2], byte_D0[0]);
  and and_55 (and_55_out, byte_D0[1], byte_D0[2], byte_D0[4]);
  and and_56 (and_56_out, byte_D0[3], byte_D0[4]);
  and and_57 (and_57_out, ~clr_sel, clr);  // And
  not not_10 (not_10_out, MEM_CLR);
  not not_11 (not_11_out, B_used);
  not not_12 (not_12_out, MEM_CLR);
  not not_13 (not_13_out, B_used);
  and and_58 (MEM_AC, or_7_out, D_accept, not_10_out, not_11_out);
  and and_59 (MEM_RD, not_12_out, not_13_out, rs_ff_5_q);
  or or_10 (or_10_out, rs_ff_5_nq, MEM_AC, MEM_CLR);
  and and_60 (and_60_out, rs_ff_6_q, or_9_out);
  and and_61 (TRAP_busy, TRAP_RD, ~TRAP_ST);  // And
  or or_11 (and_42_out[9], and_37_out, and_38_out, and_39_out);
  or or_12 (and_42_out[6], and_43_out, and_40_out, and_41_out);
  or or_13 (and_42_out[5], and_42_out[7], and_43_out, and_44_out);
  or or_14 (and_42_out[4], and_50_out, and_51_out, and_45_out);
  or or_15 (and_42_out[3], and_46_out, and_51_out, and_47_out);
  or or_16 (and_42_out[2], and_48_out, and_49_out);
  or or_17 (and_42_out[1], and_50_out, and_51_out, and_52_out);
  or or_18 (and_42_out[0], byte_D0[3], byte_D0[1], and_53_out, and_54_out);
  nor nor_5 (nor_5_out, and_55_out, and_56_out);
  ROB_FL rob_fl_1 (
    .C(C_dt), .E1(CT_ROB__FL__STA), .E2(CT_ROB__FL__STB), .D1(ROB_FL_A), .D2(ROB_FL_B), .inst1(ROB_FL_INSTA),
    .inst2(ROB_FL_INSTB), .com1(com1), .com2(com2), .com1_id(com1_inst), .com2_id(com2_inst),
    .clr_16(clr_16), .W1_O(CT_FL__W1), .D1_O(CT_FL__D1), .W2_O(CT_FL__W2), .D2_O(CT_FL__D2));
  assign CT_RF__PCSE = and_57_out ? 1'b1 : 1'bz;  // Driver driver_27
  assign CT_RF__PCJ = and_57_out ? 1'b1 : 1'bz;  // Driver driver_28
  Multiplexer #(.Bits(32)) multiplexer_7 (.sel(CT_RF__PCH), .in_0(MEM_FPC), .in_1(HALT_PC), .out(multiplexer_7_out));
  xor xor_2 (xor_2_out, STB_M__EP, LDB_M__EP);
  Comparator #(.Bits(4)) comparator_18 (
    .a(LDB_M__ID), .b(STB_M__ID), .gt(comparator_18_gt), .lt(comparator_18_lt));  // open: eq
  and and_62 (MEM_LD, or_8_out, or_10_out);
  Register #(.Bits(32)) register_12 (.D(pc_read), .C(C_dt), .en(CT_TRAP__LD), .Q(register_12_q));
  and and_63 (and_63_out, FU_CLR[4], clr, ~CT_TRAP__LD);  // And
  nor nor_6 (nor_6_out[1], byte_D1[1], nor_6_out[2]);
  nor nor_7 (nor_6_out[2], byte_D1[0], byte_D1[1], byte_D1[2]);
  and and_64 (and_64_out, byte_D0_iv[7], byte_D0_iv[6], byte_D0[5]);
  and and_65 (and_65_out, byte_D0_iv[7], byte_D0[6], byte_D0_iv[5]);
  and and_66 (and_66_out, STB_M__V, LDB_M__V);
  Multiplexer multiplexer_8 (
    .sel(xor_2_out), .in_0(comparator_18_gt), .in_1(comparator_18_lt), .out(multiplexer_8_out));
  and and_67 (and_67_out, MEM_AC, MEM_RD, not_14_out, not_15_out);
  not not_14 (not_14_out, MEM_TYPE__ST);
  not not_15 (not_15_out, MEM_LD__CLR);
  or or_19 (or_19_out, MEM_LD__REC, MEM_LD__CLR);
  assign \wait  = and_60_out ? 1'b1 : 1'bz;  // Driver driver_29
  assign CT_RF__PCH = and_60_out ? 1'b1 : 1'bz;  // Driver driver_30
  not not_16 (TRAP_free, TRAP_busy);
  and and_68 (and_68_out, byte_D0_iv[0], byte_D0_iv[1], byte_D0[2], byte_D0[3], byte_D0[4], byte_D0_iv[5], byte_D0_iv[6], byte_D0_iv[7]);
  and and_69 (and_69_out, byte_D0[1], byte_D0_iv[2], byte_D0[3], byte_D0[4], byte_D0_iv[5], byte_D0_iv[6], byte_D0_iv[7]);
  and and_70 (and_70_out, byte_D0[1], byte_D0[2], byte_D0[3], byte_D0[4], byte_D0_iv[5], byte_D0_iv[6], byte_D0_iv[7]);
  or or_20 (or_20_out[1], byte_D1[1], byte_D1[2], byte_D1[0]);
  or or_21 (or_21_out, and_65_out, and_64_out);
  and and_71 (and_71_out, com1, CT_RF__W1, ~CT_RF__EX1);  // And
  and and_72 (and_72_out, com2, CT_RF__W2, ~CT_RF__EX2);  // And
  PullDown #(.Bits(16)) pulldown_15 (.out(E_inst));
  PullDown #(.Bits(16)) pulldown_16 (.out(V1_inst));
  PullDown #(.Bits(16)) pulldown_17 (.out(V2_inst));
  PullDown pulldown_18 (.out(CT_RF__SCSRE));
  add_4c32 add_4c32_1 (.a(multiplexer_7_out), .b(4'b0100), .s(add_4c32_1_s));  // open: c
  Multiplexer #(.Bits(8)) multiplexer_9 (
    .sel(CT_BUS__IDM), .in_0(I_D__bus[31:24]), .in_1(8'h72), .out(multiplexer_9_out));
  Multiplexer multiplexer_10 (.sel(and_66_out), .in_0(STB_M__V), .in_1(multiplexer_8_out), .out(multiplexer_10_out));
  D_FF #(.Bits(32)) d_ff_6 (.D(register_12_q), .C(C_ct), .Q(HALT_PC));  // open: nQ
  RS_FF rs_ff_6 (.S(CT_TRAP__LD), .C(C_ct), .R(and_63_out), .Q(rs_ff_6_q));  // open: nQ
  and and_73 (and_73_out, byte_D0[4], byte_D0[3], byte_D0_iv[1], byte_D0_iv[2], byte_D0_iv[5], byte_D0_iv[6], byte_D0_iv[7]);
  or or_22 (or_22_out, and_68_out, and_69_out);
  and and_74 (and_74_out, BTB_JP, ~CT_RF__PCJ);  // And
  Multiplexer #(.Bits(32)) multiplexer_11 (
    .sel(and_57_out), .in_0(JPU_ADDR), .in_1(add_4c32_1_s), .out(multiplexer_11_out));
  not not_17 (not_17_out, multiplexer_10_out);
  Multiplexer #(.Bits(32)) multiplexer_12 (
    .sel(multiplexer_10_out), .in_0(LDB_M__A), .in_1(STB_M__A), .out(multiplexer_12_out));
  Multiplexer #(.Bits(2)) multiplexer_13 (
    .sel(multiplexer_10_out), .in_0(LDB_M__MD), .in_1(STB_M__MD), .out(multiplexer_13_out));
  and and_75 (and_75_out, or_19_out, ~and_67_out);  // And
  and and_76 (and_76_out, and_70_out, byte_D0[0]);
  and and_77 (and_77_out, byte_D0_iv[0], and_70_out);
  // regFile4 regfile4_1: pin names not known; wires that end beside it: C_dt, and_71_out, and_72_out, CT_RF__D1, CT_RF__D2, CT_RF__R1[7:3], CT_RF__R1[2:0], CT_RF__R2[7:3], CT_RF__R2[2:0], CT_RF__RA, CT_RF__MA, CT_RF__RB, CT_RF__MB, pcs_i, CT_RF__PCSE, pca_i, CT_RF__PCAE, ISC_sc, CT_RF__SCSS, CT_RF__SCSE, sca_i, CT_RF__SCAE, CT_RF__SCAE, {{23{1'b0}}, FL[14], fl_i}, CT_RF__FLS, 4'b0001, pc_read, R_A, R_B, PCS, PCA, SCS, SCA, FL
  or or_23 (or_23_out[0], CT_RF__PCH, CT_RF__PCJ);
  or or_24 (or_23_out[1], CT_RF__PCH, and_74_out);
  add_4c32 add_4c32_2 (.a(PCS), .b(4'b0100), .s(add_4c32_2_s));  // open: c
  Register #(.Bits(37)) BTB_F (
    .D({BTB_packet[36:3], BTB_JP, BTB_packet[1:0]}), .C(C_dt), .en(CT_BUS__IAR), .Q(BTB_fetch));
  Register #(.Bits(32)) I_A__R (.D(PCS), .C(C_dt), .en(CT_BUS__IAR), .Q(I_A__R_q));
  Register #(.Bits(32)) I_D__R (.D({multiplexer_9_out, I_D__bus[23:0]}), .C(C_dt), .en(dc_e), .Q(I_D__R_q));
  Register #(.Bits(37)) BTB_D (.D(BTB_fetch), .C(C_dt), .en(dc_e), .Q(BTB_D_q));
  and and_78 (MB_LDB__LD, LDB_M__V, MEM_LD, not_17_out);
  and and_79 (MB_STB__LD, multiplexer_10_out, MEM_LD);
  Register register_13 (.D(multiplexer_10_out), .C(C_dt), .en(MEM_LD), .Q(MEM_TYPE__ST));
  Register register_14 (.D(LDB_M__EP), .C(C_dt), .en(MEM_LD), .Q(MEM_EP));
  Register #(.Bits(4)) register_15 (.D(LDB_M__ID), .C(C_dt), .en(MEM_LD), .Q(MEM_INST));
  Register #(.Bits(32)) register_16 (.D(multiplexer_12_out), .C(C_dt), .en(MEM_LD), .Q(register_16_q));
  Register #(.Bits(2)) register_17 (.D(multiplexer_13_out), .C(C_dt), .en(MEM_LD), .Q(register_17_q));
  Register #(.Bits(32)) register_18 (.D(STB_M__D), .C(C_dt), .en(MEM_LD), .Q(register_18_q));
  not not_18 (not_18_out, MEM_LD__CLR);
  RS_FF rs_ff_7 (.S(and_67_out), .C(C_dt), .R(and_75_out), .Q(rs_ff_7_q), .nQ(rs_ff_7_nq));
  Register #(.Bits(32)) register_19 (.D(D_D__bus), .C(C_dt), .en(MEM_AC), .Q(MEM_LD__D));
  Register #(.Bits(4)) register_20 (.D(MEM_INST), .C(C_dt), .en(MEM_AC), .Q(MEM_LD__INST));
  Register register_21 (.D(MEM_EP), .C(C_dt), .en(MEM_AC), .Q(MEM_LD__EP));
  and and_80 (and_80_out, byte_D0_iv[7], byte_D0_iv[6], byte_D0_iv[5], byte_D0_iv[4]);
  and and_81 (and_81_out, byte_D0_iv[7], byte_D0_iv[6], byte_D0_iv[5], byte_D0[4], byte_D0_iv[3]);
  assign {CT_RF__RA, CT_RF__MA} = or_27_out ? byte_D1 : 8'bz;  // Driver driver_31
  assign {CT_RF__RB, CT_RF__MB} = or_27_out ? byte_D2 : 8'bz;  // Driver driver_32
  assign CT_ALU__LD = or_27_out ? CT_DISP : 1'bz;  // Driver driver_33
  assign CT_ALU__CT = or_27_out ? {1'b0, and_42_out[7:0]} : 9'bz;  // Driver driver_34
  assign CT_ALU__M = or_27_out ? and_42_out[9] : 1'bz;  // Driver driver_35
  assign CT_FU__INST = or_27_out ? inst_DP : 4'bz;  // Driver driver_36
  assign CT_FU__EPOCH = or_27_out ? epoch_DP : 1'bz;  // Driver driver_37
  assign CT_FU__WR = or_27_out ? byte_D1 : 8'bz;  // Driver driver_38
  assign CT_ALU__WD = or_27_out ? nor_5_out : 1'bz;  // Driver driver_39
  assign CT_ALU__WF = or_27_out ? 1'b1 : 1'bz;  // Driver driver_40
  assign {CT_RF__RA, CT_RF__MA} = or_22_out ? byte_D2 : 8'bz;  // Driver driver_41
  assign CT_DIR__LD = or_22_out ? CT_DISP : 1'bz;  // Driver driver_42
  assign CT_DIR__M = or_22_out ? and_69_out : 1'bz;  // Driver driver_43
  assign CT_DIR__MS = or_22_out ? byte_D0[0] : 1'bz;  // Driver driver_44
  assign CT_FU__INST = or_22_out ? inst_DP : 4'bz;  // Driver driver_45
  assign CT_FU__EPOCH = or_22_out ? epoch_DP : 1'bz;  // Driver driver_46
  assign CT_FU__WR = or_22_out ? byte_D1 : 8'bz;  // Driver driver_47
  assign CT_RF__SCSS = and_70_out ? 1'b1 : 1'bz;  // Driver driver_48
  assign {CT_RF__RB, CT_RF__MB} = and_70_out ? 8'hf0 : 8'bz;  // Driver driver_49
  assign {CT_RF__RA, CT_RF__MA} = and_76_out ? byte_D1 : 8'bz;  // Driver driver_50
  assign CT_FU__WR = and_77_out ? byte_D1 : 8'bz;  // Driver driver_51
  assign CT_MB__LD = and_70_out ? CT_DISP : 1'bz;  // Driver driver_52
  assign CT_MB__ST = and_76_out ? 1'b1 : 1'bz;  // Driver driver_53
  assign CT_SP__MOF = and_76_out ? {1'b1, or_20_out[1], byte_D1[1]} : 3'bz;  // Driver driver_54
  assign CT_MB__OFFM = and_70_out ? 1'b1 : 1'bz;  // Driver driver_55
  assign CT_RF__SCSE = and_70_out ? 1'b1 : 1'bz;  // Driver driver_56
  assign CT_RF__SCN = and_70_out ? {nor_6_out, byte_D1[1]} : 3'bz;  // Driver driver_57
  assign CT_RF__SCD = and_76_out ? 1'b1 : 1'bz;  // Driver driver_58
  assign CT_FU__INST = and_70_out ? inst_DP : 4'bz;  // Driver driver_59
  assign CT_FU__EPOCH = and_70_out ? epoch_DP : 1'bz;  // Driver driver_60
  assign CT_RF__SCSRE = and_70_out ? 1'b1 : 1'bz;  // Driver driver_61
  assign CT_FU__EPOCH = or_21_out ? epoch_DP : 1'bz;  // Driver driver_62
  assign CT_FU__INST = or_21_out ? inst_DP : 4'bz;  // Driver driver_63
  assign {CT_RF__RB, CT_RF__MB} = or_21_out ? {byte_D0[4:0], 3'b000} : 8'bz;  // Driver driver_64
  assign {CT_RF__RA, CT_RF__MA} = and_65_out ? byte_D1 : 8'bz;  // Driver driver_65
  assign CT_FU__WR = and_64_out ? byte_D1 : 8'bz;  // Driver driver_66
  assign CT_MB__LD = or_21_out ? CT_DISP : 1'bz;  // Driver driver_67
  assign CT_MB__ST = and_65_out ? 1'b1 : 1'bz;  // Driver driver_68
  or or_25 (CT_RF__PCAE, com1, com2);
  ROB_INT rob_int_1 (
    .C(C_dt), .E1(CT_ROB__INT__STA), .E2(CT_ROB__INT__STB), .D1(ROB_INT_A), .D2(ROB_INT_B),
    .inst1(ROB_INT_INSTA), .inst2(ROB_INT_INSTB), .com1(com1), .com2(com2), .com1_id(com1_inst),
    .com2_id(com2_inst), .clr_16(clr_16), .W_O(CT_INT__W), .D_O(CT_INT__D));
  Multiplexer #(.Selector_Bits(2), .Bits(32)) multiplexer_14 (
    .sel(or_23_out), .in_0(add_4c32_2_s), .in_1(multiplexer_11_out), .in_2(BTB_packet[36:5]),
    .in_3(add_4c32_1_s), .out(pcs_i));
  assign I_A__bus = CT_BUS__IAG ? I_A__R_q : 32'bz;  // Driver driver_69
  D_FF #(.Bits(32)) d_ff_7 (.D(I_D__R_q), .C(C_ct), .Q({byte_I0, byte_I1, byte_I2, byte_I3}));  // open: nQ
  D_FF #(.Bits(37)) d_ff_8 (.D(BTB_D_q), .C(C_ct), .Q(BTB_pack__iss));  // open: nQ
  assign D_A__bus = MEM_RD ? register_16_q : 32'bz;  // Driver driver_70
  assign D_MD = MEM_RD ? register_17_q : 2'bz;  // Driver driver_71
  assign D_D__bus = D_ST ? register_18_q : 32'bz;  // Driver driver_72
  and and_82 (MEM_LD__RD, not_18_out, rs_ff_7_q);
  or or_26 (MEM_BF__free, rs_ff_7_nq, MEM_LD__RD, MEM_LD__CLR);
  RS_FF u_HLT (.S(run_t), .C(C_ct), .R(hlt), .nQ(halted));  // open: Q
  Register register_22 (.D(CT_KILL), .C(C_ct), .en(CT_TRAP__LD), .Q(hlt));
  PullDown pulldown_19 (.out(CT_INT));
  PullDown #(.Bits(8)) pulldown_20 (.out(CT_INTID));
  and and_83 (D_LD, ~MEM_TYPE__ST, MEM_RD);  // And
  and and_84 (D_ST, MEM_RD, MEM_TYPE__ST);
  or or_27 (or_27_out, and_80_out, and_73_out, and_81_out);
  BitExtender #(.inputBits(1), .outputBits(8)) bitextender_3 (.in(byte_D0[3]), .out(bitextender_3_out));
  assign xor_3_out = FL[7:0] ^ bitextender_3_out;  // XOr xor_3, 8 bits wide
  and and_85 (and_85_out, com1, CT_SC__W1);
  and and_86 (and_86_out, com2, CT_SC__W2);
  and and_87 (and_87_out, byte_D2[7], CT_DIR__MS);
  BitExtender #(.inputBits(1)) bitextender_4 (.in(and_87_out), .out(bitextender_4_out));
  and and_88 (and_88_out, byte_D0[1], byte_D0_iv[2], byte_D0[3], byte_D0[4], byte_D0[5], byte_D0[6], byte_D0_iv[7]);
  assign CT_RF__SCSE = clr ? 1'b1 : 1'bz;  // Driver driver_73
  assign CT_RF__SCSS = clr ? 1'b1 : 1'bz;  // Driver driver_74
  Multiplexer multiplexer_15 (.sel(and_100_out[2]), .in_0(nand_1_out[2]), .in_1(1'b1), .out(multiplexer_15_out));
  not not_19 (not_19_out[0], register_23_q[0]);
  xor xor_4 (not_19_out[1], register_23_q[0], register_23_q[1]);
  xor xor_5 (not_19_out[2], register_23_q[1], register_23_q[2]);
  Multiplexer #(.Bits(32)) multiplexer_16 (
    .sel(CT_ALU__M), .in_0(R_B), .in_1({{16{1'b0}}, byte_D2, byte_D3}), .out(multiplexer_16_out));
  PullDown #(.Bits(8)) pulldown_21 (.out(CT_DIR__EXID));
  PullDown pulldown_22 (.out(CT_DIR__EXM));
  PullDown pulldown_23 (.out(CT_FU__EX));
  and and_89 (and_89_out, byte_D0_iv[4], byte_D0[5], byte_D0[6], byte_D0_iv[7]);
  Multiplexer #(.Selector_Bits(3)) multiplexer_17 (
    .sel(byte_D0[2:0]), .in_0(xor_3_out[0]), .in_1(xor_3_out[1]), .in_2(xor_3_out[2]), .in_3(xor_3_out[3]),
    .in_4(xor_3_out[4]), .in_5(xor_3_out[5]), .in_6(xor_3_out[6]), .in_7(xor_3_out[7]),
    .out(multiplexer_17_out));
  or or_28 (CT_RF__SCAE, and_85_out, and_86_out);
  and and_90 (and_90_out, multiplexer_15_out, CT_ALU__LD);
  Register register_23 (.D(and_90_out), .C(C_ct), .en(or_29_out), .Q(register_23_q[2]));
  not not_20 (not_20_out, multiplexer_15_out);
  or or_29 (or_29_out, not_20_out, multiplexer_18_out[2]);
  Multiplexer #(.Bits(3)) multiplexer_18 (
    .sel(or_30_out), .in_0(not_19_out), .in_1(and_100_out), .out(multiplexer_18_out));
  or or_30 (or_30_out, and_100_out[0], and_100_out[1], and_100_out[2]);
  Register #(.Bits(4)) register_24 (.D(CT_FU__INST), .C(C_ct), .en(multiplexer_18_out[2]), .Q(register_24_q));
  Register register_25 (.D(CT_FU__EPOCH), .C(C_ct), .en(multiplexer_18_out[2]), .Q(register_25_q));
  Register register_26 (.D(CT_ALU__WD), .C(C_ct), .en(multiplexer_18_out[2]), .Q(register_26_q));
  Register register_27 (.D(CT_ALU__WF), .C(C_ct), .en(multiplexer_18_out[2]), .Q(register_27_q));
  Register #(.Bits(32)) register_28 (.D(R_A), .C(C_dt), .en(multiplexer_18_out[2]), .Q(register_28_q));
  Register #(.Bits(32)) register_29 (.D(multiplexer_16_out), .C(C_dt), .en(multiplexer_18_out[2]), .Q(register_29_q));
  Register #(.Bits(8)) register_30 (.D(FL[7:0]), .C(C_dt), .en(multiplexer_18_out[2]), .Q(register_30_q));
  Register #(.Bits(9)) register_31 (.D(CT_ALU__CT), .C(C_ct), .en(multiplexer_18_out[2]), .Q(register_31_q));
  Register #(.Bits(8)) register_32 (.D(CT_FU__WR), .C(C_ct), .en(multiplexer_18_out[2]), .Q(register_32_q));
  Multiplexer #(.Bits(32)) multiplexer_19 (
    .sel(CT_DIR__M), .in_0(R_A), .in_1({bitextender_4_out, byte_D2, byte_D3}), .out(multiplexer_19_out));
  or or_31 (or_31_out, CT_FU__WR[0], CT_FU__WR[2]);
  not not_21 (not_21_out, CT_FU__WR[1]);
  and and_91 (and_91_out, byte_D0_iv[0], byte_D0_iv[1], byte_D0_iv[2], byte_D0_iv[3], byte_D0[4], byte_D0[5], byte_D0[6], byte_D0_iv[7]);
  and and_92 (and_92_out, byte_D0[0], byte_D0_iv[1], byte_D0_iv[2], byte_D0_iv[3], byte_D0[4], byte_D0[5], byte_D0[6], byte_D0_iv[7]);
  and and_93 (and_93_out, byte_D0_iv[1], byte_D0[2], byte_D0_iv[3], byte_D0[4], byte_D0[5], byte_D0[6], byte_D0_iv[7]);
  and and_94 (and_94_out, byte_D0[0], byte_D0_iv[1], byte_D0[2], byte_D0[3], byte_D0[4], byte_D0_iv[5], byte_D0_iv[6], byte_D0_iv[7]);
  and and_95 (and_95_out, byte_D0[0], and_88_out);
  and and_96 (and_96_out, and_88_out, byte_D0_iv[0]);
  Multiplexer multiplexer_20 (
    .sel(and_100_out[1]), .in_0(nand_1_out[1]), .in_1(nand_1_out[2]), .out(multiplexer_20_out));
  Multiplexer multiplexer_21 (
    .sel(register_23_q[2]), .in_0(CT_ALU__LD), .in_1(register_23_q[2]), .out(multiplexer_21_out));
  Multiplexer #(.Bits(4)) multiplexer_22 (
    .sel(register_23_q[2]), .in_0(CT_FU__INST), .in_1(register_24_q), .out(multiplexer_22_out));
  inst_comp inst_comp_4 (
    .A_id(register_24_q), .A_ep(register_25_q), .B_id(clr_id), .B_ep(clr_ep), .A_new(inst_comp_4_a_new));
  Multiplexer multiplexer_23 (
    .sel(register_23_q[2]), .in_0(CT_FU__EPOCH), .in_1(register_25_q), .out(multiplexer_23_out));
  Multiplexer multiplexer_24 (
    .sel(register_23_q[2]), .in_0(CT_ALU__WD), .in_1(register_26_q), .out(multiplexer_24_out));
  Multiplexer multiplexer_25 (
    .sel(register_23_q[2]), .in_0(CT_ALU__WF), .in_1(register_27_q), .out(multiplexer_25_out));
  Multiplexer #(.Bits(32)) multiplexer_26 (
    .sel(register_23_q[2]), .in_0(R_A), .in_1(register_28_q), .out(multiplexer_26_out));
  Multiplexer #(.Bits(32)) multiplexer_27 (
    .sel(register_23_q[2]), .in_0(multiplexer_16_out), .in_1(register_29_q), .out(multiplexer_27_out));
  Multiplexer #(.Bits(8)) multiplexer_28 (
    .sel(register_23_q[2]), .in_0(FL[7:0]), .in_1(register_30_q), .out(multiplexer_28_out));
  Multiplexer #(.Bits(9)) multiplexer_29 (
    .sel(register_23_q[2]), .in_0(CT_ALU__CT), .in_1(register_31_q), .out(multiplexer_29_out));
  Multiplexer #(.Bits(8)) multiplexer_30 (
    .sel(register_23_q[2]), .in_0(CT_FU__WR), .in_1(register_32_q), .out(multiplexer_30_out));
  Multiplexer multiplexer_31 (.sel(and_104_out[2]), .in_0(nand_4_out[2]), .in_1(1'b1), .out(multiplexer_31_out));
  not not_22 (not_22_out[0], register_48_q[0]);
  xor xor_6 (not_22_out[1], register_48_q[0], register_48_q[1]);
  xor xor_7 (not_22_out[2], register_48_q[1], register_48_q[2]);
  Multiplexer #(.Bits(32)) multiplexer_32 (
    .sel(CT_DIR__EXM), .in_0(multiplexer_19_out), .in_1(RX_SEL), .out(multiplexer_32_out));
  Multiplexer #(.Bits(32)) multiplexer_33 (.sel(CT_INTM), .in_0(R_A), .in_1(int_pc), .out(multiplexer_33_out));
  add_4c32 add_4c32_3 (.a(pc_read), .b(4'b0100), .s(add_4c32_3_s));  // open: c
  BitExtender #(.inputBits(3)) bitextender_5 (.in(CT_SP__MOF), .out(bitextender_5_out));
  and and_97 (and_97_out[0], or_31_out, not_21_out);
  and and_98 (and_98_out, multiplexer_20_out, multiplexer_21_out);
  not not_23 (not_23_out, multiplexer_20_out);
  or or_32 (or_32_out, not_23_out, multiplexer_18_out[1]);
  or or_33 (register_23_q[1], register_47_q[1], register_23_q[2]);
  nand nand_1 (nand_1_out[2], inst_comp_4_a_new, register_23_q[2], clr);
  Register #(.Bits(4)) register_33 (.D(multiplexer_22_out), .C(C_ct), .en(multiplexer_18_out[1]), .Q(register_33_q));
  Register register_34 (.D(multiplexer_23_out), .C(C_ct), .en(multiplexer_18_out[1]), .Q(register_34_q));
  Register register_35 (.D(multiplexer_24_out), .C(C_ct), .en(multiplexer_18_out[1]), .Q(register_35_q));
  Register register_36 (.D(multiplexer_25_out), .C(C_ct), .en(multiplexer_18_out[1]), .Q(register_36_q));
  Register #(.Bits(32)) register_37 (.D(multiplexer_26_out), .C(C_dt), .en(multiplexer_18_out[1]), .Q(register_37_q));
  Register #(.Bits(32)) register_38 (.D(multiplexer_27_out), .C(C_dt), .en(multiplexer_18_out[1]), .Q(register_38_q));
  Register #(.Bits(8)) register_39 (.D(multiplexer_28_out), .C(C_dt), .en(multiplexer_18_out[1]), .Q(register_39_q));
  Register #(.Bits(9)) register_40 (.D(multiplexer_29_out), .C(C_ct), .en(multiplexer_18_out[1]), .Q(register_40_q));
  Register #(.Bits(8)) register_41 (.D(multiplexer_30_out), .C(C_ct), .en(multiplexer_18_out[1]), .Q(register_41_q));
  and and_99 (and_99_out, multiplexer_31_out, CT_DIR__LD);
  not not_24 (not_24_out, multiplexer_31_out);
  Register #(.Bits(4)) register_42 (.D(CT_FU__INST), .C(C_ct), .en(multiplexer_47_out[2]), .Q(register_42_q));
  Register register_43 (.D(CT_FU__EPOCH), .C(C_ct), .en(multiplexer_47_out[2]), .Q(register_43_q));
  Register #(.Bits(32)) register_44 (.D(multiplexer_32_out), .C(C_dt), .en(multiplexer_47_out[2]), .Q(register_44_q));
  Register #(.Bits(8)) register_45 (.D(CT_FU__WR), .C(C_ct), .en(multiplexer_47_out[2]), .Q(register_45_q));
  Register register_46 (.D(CT_FU__EX), .C(C_ct), .en(multiplexer_47_out[2]), .Q(register_46_q));
  Multiplexer #(.Bits(32)) multiplexer_34 (
    .sel(CT_CALLM), .in_0(multiplexer_33_out), .in_1(add_4c32_3_s), .out(multiplexer_34_out));
  Multiplexer #(.Bits(32)) multiplexer_35 (.sel(CT_INTM), .in_0(R_B), .in_1(ISC), .out(multiplexer_35_out));
  Multiplexer #(.Bits(16)) multiplexer_36 (
    .sel(CT_MB__OFFM), .in_0({byte_D2, byte_D3}), .in_1(bitextender_5_out), .out(multiplexer_36_out));
  assign CT_FU__EPOCH = and_89_out ? epoch_DP : 1'bz;  // Driver driver_75
  assign CT_FU__INST = and_89_out ? inst_DP : 4'bz;  // Driver driver_76
  assign {CT_RF__RA, CT_RF__MA} = and_89_out ? byte_D1 : 8'bz;  // Driver driver_77
  assign CT_JPU__LD = and_89_out ? CT_DISP : 1'bz;  // Driver driver_78
  assign CT_JPU__JP = and_89_out ? multiplexer_17_out : 1'bz;  // Driver driver_79
  assign JPU_A__ST = and_89_out ? 1'b1 : 1'bz;  // Driver driver_80
  assign CT_FU__EPOCH = and_91_out ? epoch_DP : 1'bz;  // Driver driver_81
  assign CT_FU__INST = and_91_out ? inst_DP : 4'bz;  // Driver driver_82
  assign {CT_RF__RA, CT_RF__MA} = and_91_out ? byte_D1 : 8'bz;  // Driver driver_83
  assign {CT_RF__RB, CT_RF__MB} = and_91_out ? 8'hf0 : 8'bz;  // Driver driver_84
  assign CT_JPU__LD = and_91_out ? 1'b1 : 1'bz;  // Driver driver_85
  assign CT_JPU__JP = and_91_out ? CT_DISP : 1'bz;  // Driver driver_86
  assign JPU_A__ST = and_91_out ? 1'b1 : 1'bz;  // Driver driver_87
  assign CT_MB__LD = and_91_out ? 1'b1 : 1'bz;  // Driver driver_88
  assign CT_MB__ST = and_91_out ? 1'b1 : 1'bz;  // Driver driver_89
  assign CT_CALLM = and_91_out ? 1'b1 : 1'bz;  // Driver driver_90
  assign CT_SP__MOF = and_91_out ? 3'b100 : 3'bz;  // Driver driver_91
  assign CT_MB__OFFM = and_91_out ? 1'b1 : 1'bz;  // Driver driver_92
  assign CT_RF__SCSE = and_91_out ? 1'b1 : 1'bz;  // Driver driver_93
  assign CT_RF__SCSS = and_91_out ? 1'b1 : 1'bz;  // Driver driver_94
  assign CT_RF__SCD = and_91_out ? 1'b1 : 1'bz;  // Driver driver_95
  assign CT_RF__SCN = and_91_out ? 3'b100 : 3'bz;  // Driver driver_96
  assign CT_FU__MF = and_91_out ? 1'b1 : 1'bz;  // Driver driver_97
  assign JPU_CALL = and_91_out ? 1'b1 : 1'bz;  // Driver driver_98
  assign CT_RF__SCSRE = and_91_out ? 1'b1 : 1'bz;  // Driver driver_99
  assign CT_FU__EPOCH = and_92_out ? epoch_DP : 1'bz;  // Driver driver_100
  assign CT_FU__INST = and_92_out ? inst_DP : 4'bz;  // Driver driver_101
  assign {CT_RF__RB, CT_RF__MB} = and_92_out ? 8'hf0 : 8'bz;  // Driver driver_102
  assign CT_FU__WR = and_92_out ? 8'he8 : 8'bz;  // Driver driver_103
  assign CT_MB__LD = and_92_out ? 1'b1 : 1'bz;  // Driver driver_104
  assign CT_MB__OFFM = and_92_out ? 1'b1 : 1'bz;  // Driver driver_105
  assign CT_RF__SCSE = and_92_out ? 1'b1 : 1'bz;  // Driver driver_106
  assign CT_RF__SCSS = and_92_out ? 1'b1 : 1'bz;  // Driver driver_107
  assign CT_RF__SCN = and_92_out ? 3'b100 : 3'bz;  // Driver driver_108
  assign CT_FU__MF = and_92_out ? 1'b1 : 1'bz;  // Driver driver_109
  assign CT_RET__LD = and_92_out ? 1'b1 : 1'bz;  // Driver driver_110
  assign CT_RF__SCSRE = and_92_out ? 1'b1 : 1'bz;  // Driver driver_111
  assign CT_KILL = and_93_out ? byte_D0[0] : 1'bz;  // Driver driver_112
  assign CT_FU__EPOCH = and_93_out ? epoch_DP : 1'bz;  // Driver driver_113
  assign CT_FU__INST = and_93_out ? inst_DP : 4'bz;  // Driver driver_114
  assign CT_TRAP__LD = and_93_out ? 1'b1 : 1'bz;  // Driver driver_115
  bus16x2_demux bus16x2_demux_2 (.bus_1(V1_inst), .bus_2(V2_inst), .E(and_94_out), .id(inst_DP));
  assign CT_FU__WR = and_95_out ? byte_D3 : 8'bz;  // Driver driver_116
  assign {CT_RF__RA, CT_RF__MA} = and_95_out ? byte_D1 : 8'bz;  // Driver driver_117
  assign CT_DIR__LD = and_88_out ? CT_DISP : 1'bz;  // Driver driver_118
  assign CT_FU__INST = and_88_out ? inst_DP : 4'bz;  // Driver driver_119
  assign CT_FU__EPOCH = and_88_out ? epoch_DP : 1'bz;  // Driver driver_120
  assign CT_FU__WR = and_96_out ? byte_D1 : 8'bz;  // Driver driver_121
  assign CT_DIR__EXID = and_96_out ? byte_D3 : 8'bz;  // Driver driver_122
  assign CT_DIR__EXM = and_88_out ? 1'b1 : 1'bz;  // Driver driver_123
  assign CT_FU__EX = and_88_out ? 1'b1 : 1'bz;  // Driver driver_124
  Multiplexer #(.Bits(32)) multiplexer_37 (.sel(CT_ISCCM), .in_0(SCS), .in_1(ISC), .out(multiplexer_37_out));
  Register register_47 (.D(and_98_out), .C(C_ct), .en(or_32_out), .Q(register_47_q[1]));
  or or_34 (register_23_q[0], ALU_busy, register_47_q[1], register_23_q[2]);
  assign and_100_out = nand_2_out & register_23_q;  // And and_100, 3 bits wide
  Multiplexer #(.Bits(4)) multiplexer_38 (
    .sel(register_23_q[1]), .in_0(CT_FU__INST), .in_1(register_33_q), .out(multiplexer_38_out));
  inst_comp inst_comp_5 (
    .A_id(register_33_q), .A_ep(register_34_q), .B_id(clr_id), .B_ep(clr_ep), .A_new(inst_comp_5_a_new));
  Multiplexer multiplexer_39 (
    .sel(register_23_q[1]), .in_0(CT_FU__EPOCH), .in_1(register_34_q), .out(multiplexer_39_out));
  Multiplexer multiplexer_40 (
    .sel(register_23_q[1]), .in_0(CT_ALU__WD), .in_1(register_35_q), .out(multiplexer_40_out));
  Multiplexer multiplexer_41 (
    .sel(register_23_q[1]), .in_0(CT_ALU__WF), .in_1(register_36_q), .out(multiplexer_41_out));
  Multiplexer #(.Bits(32)) multiplexer_42 (
    .sel(register_23_q[1]), .in_0(R_A), .in_1(register_37_q), .out(multiplexer_42_out));
  Multiplexer #(.Bits(32)) multiplexer_43 (
    .sel(register_23_q[1]), .in_0(multiplexer_16_out), .in_1(register_38_q), .out(multiplexer_43_out));
  Multiplexer #(.Bits(8)) multiplexer_44 (
    .sel(register_23_q[1]), .in_0(FL[7:0]), .in_1(register_39_q), .out(multiplexer_44_out));
  Multiplexer #(.Bits(9)) multiplexer_45 (
    .sel(register_23_q[1]), .in_0(CT_ALU__CT), .in_1(register_40_q), .out(multiplexer_45_out));
  Multiplexer #(.Bits(8)) multiplexer_46 (
    .sel(register_23_q[1]), .in_0(CT_FU__WR), .in_1(register_41_q), .out(multiplexer_46_out));
  Register register_48 (.D(and_99_out), .C(C_ct), .en(or_35_out), .Q(register_48_q[2]));
  or or_35 (or_35_out, not_24_out, multiplexer_47_out[2]);
  Multiplexer #(.Bits(3)) multiplexer_47 (
    .sel(or_36_out), .in_0(not_22_out), .in_1(and_104_out), .out(multiplexer_47_out));
  or or_36 (or_36_out, and_104_out[0], and_104_out[1], and_104_out[2]);
  Multiplexer #(.Bits(4)) multiplexer_48 (
    .sel(register_48_q[2]), .in_0(CT_FU__INST), .in_1(register_42_q), .out(multiplexer_48_out));
  inst_comp inst_comp_6 (
    .A_id(register_42_q), .A_ep(register_43_q), .B_id(clr_id), .B_ep(clr_ep), .A_new(inst_comp_6_a_new));
  Multiplexer multiplexer_49 (
    .sel(register_48_q[2]), .in_0(CT_FU__EPOCH), .in_1(register_43_q), .out(multiplexer_49_out));
  Multiplexer #(.Bits(32)) multiplexer_50 (
    .sel(register_48_q[2]), .in_0(multiplexer_32_out), .in_1(register_44_q), .out(multiplexer_50_out));
  Multiplexer #(.Bits(8)) multiplexer_51 (
    .sel(register_48_q[2]), .in_0(CT_FU__WR), .in_1(register_45_q), .out(multiplexer_51_out));
  Multiplexer multiplexer_52 (.sel(register_48_q[2]), .in_0(CT_FU__EX), .in_1(register_46_q), .out(multiplexer_52_out));
  and and_101 (MB_LD, MB_free, CT_MB__LD);
  Register register_49 (.D(CT_MB__LD), .C(C_ct), .en(1'b1), .Q(register_49_q));
  Register #(.Bits(4)) register_50 (.D(CT_FU__INST), .C(C_ct), .en(MB_LD), .Q(MB_INST));
  Register register_51 (.D(CT_FU__EPOCH), .C(C_ct), .en(MB_LD), .Q(MB_ep));
  Register register_52 (.D(CT_MB__ST), .C(C_ct), .en(MB_LD), .Q(MB_type__st));
  Register #(.Bits(32)) register_53 (.D(multiplexer_34_out), .C(C_dt), .en(MB_LD), .Q(MB_data));
  Register #(.Bits(32)) register_54 (.D(multiplexer_35_out), .C(C_dt), .en(MB_LD), .Q(register_54_q));
  Register #(.Bits(16)) register_55 (.D(multiplexer_36_out), .C(C_dt), .en(MB_LD), .Q(register_55_q));
  Register #(.Bits(2)) register_56 (.D({CT_FU__WR[1], and_97_out[0]}), .C(C_ct), .en(MB_LD), .Q(MB_MD));
  Register #(.Bits(8)) register_57 (.D(CT_FU__WR), .C(C_ct), .en(MB_LD), .Q(MB_WR));
  Register register_58 (.D(CT_FU__MF), .C(C_ct), .en(MB_LD), .Q(MB_MF));
  Register #(.Bits(32)) register_59 (.D(pc_read), .C(C_dt), .en(MB_LD), .Q(MB_PC));
  Multiplexer #(.Bits(32)) multiplexer_53 (.sel(and_86_out), .in_0(CT_SC__D1), .in_1(CT_SC__D2), .out(sca_i));
  Multiplexer multiplexer_54 (
    .sel(and_100_out[0]), .in_0(nand_1_out[0]), .in_1(nand_1_out[1]), .out(multiplexer_54_out));
  Multiplexer multiplexer_55 (
    .sel(register_23_q[1]), .in_0(CT_ALU__LD), .in_1(register_47_q[1]), .out(multiplexer_55_out));
  and and_102 (and_102_out, multiplexer_54_out, multiplexer_55_out);
  nand nand_2 (nand_2_out[2], ALU_busy, register_47_q[1], register_23_q[2]);
  nand nand_3 (nand_1_out[1], inst_comp_5_a_new, register_47_q[1], clr);
  Register #(.Bits(4)) register_60 (.D(multiplexer_38_out), .C(C_ct), .en(ALU_A_LD), .Q(ALU_A_INST));
  Register register_61 (.D(multiplexer_39_out), .C(C_ct), .en(ALU_A_LD), .Q(register_61_q));
  Register #(.Bits(32)) register_62 (.D(multiplexer_42_out), .C(C_dt), .en(ALU_A_LD), .Q(ALU_A_A));
  Register #(.Bits(32)) register_63 (.D(multiplexer_43_out), .C(C_dt), .en(ALU_A_LD), .Q(ALU_A_B));
  Register #(.Bits(8)) register_64 (.D(multiplexer_44_out), .C(C_dt), .en(ALU_A_LD), .Q(ALU_A_FI));
  Register #(.Bits(9)) register_65 (.D(multiplexer_45_out), .C(C_ct), .en(ALU_A_LD), .Q(ALU_A_CT));
  Register #(.Bits(8)) register_66 (.D(multiplexer_46_out), .C(C_ct), .en(ALU_A_LD), .Q({ALU_A_WR, ALU_A_RM}));
  Multiplexer multiplexer_56 (
    .sel(and_104_out[1]), .in_0(nand_4_out[1]), .in_1(nand_4_out[2]), .out(multiplexer_56_out));
  Multiplexer multiplexer_57 (
    .sel(register_48_q[2]), .in_0(CT_DIR__LD), .in_1(register_48_q[2]), .out(multiplexer_57_out));
  and and_103 (and_103_out, multiplexer_56_out, multiplexer_57_out);
  not not_25 (not_25_out, multiplexer_56_out);
  nand nand_4 (nand_4_out[2], inst_comp_6_a_new, register_48_q[2], clr);
  Register #(.Bits(4)) register_67 (.D(multiplexer_48_out), .C(C_ct), .en(multiplexer_47_out[1]), .Q(register_67_q));
  Register register_68 (.D(multiplexer_49_out), .C(C_ct), .en(multiplexer_47_out[1]), .Q(register_68_q));
  Register #(.Bits(32)) register_69 (.D(multiplexer_50_out), .C(C_dt), .en(multiplexer_47_out[1]), .Q(register_69_q));
  Register #(.Bits(8)) register_70 (.D(multiplexer_51_out), .C(C_ct), .en(multiplexer_47_out[1]), .Q(register_70_q));
  Register register_71 (.D(multiplexer_52_out), .C(C_ct), .en(multiplexer_47_out[1]), .Q(register_71_q));
  addsub_4c32 addsub_4c32_1 (
    .a(multiplexer_37_out), .b({1'b0, CT_RF__SCN}), .sub(CT_RF__SCD), .s(addsub_4c32_1_s));  // open: c
  nand nand_5 (nand_2_out[1], ALU_busy, register_47_q[1]);
  Register register_72 (.D(and_103_out), .C(C_ct), .en(or_37_out), .Q(register_72_q[1]));
  or or_37 (or_37_out, not_25_out, multiplexer_47_out[1]);
  or or_38 (register_48_q[1], register_72_q[1], register_48_q[2]);
  assign and_104_out = nand_8_out & register_48_q;  // And and_104, 3 bits wide
  Multiplexer #(.Bits(4)) multiplexer_58 (
    .sel(register_48_q[1]), .in_0(CT_FU__INST), .in_1(register_67_q), .out(multiplexer_58_out));
  inst_comp inst_comp_7 (
    .A_id(register_67_q), .A_ep(register_68_q), .B_id(clr_id), .B_ep(clr_ep), .A_new(inst_comp_7_a_new));
  Multiplexer multiplexer_59 (
    .sel(register_48_q[1]), .in_0(CT_FU__EPOCH), .in_1(register_68_q), .out(multiplexer_59_out));
  Multiplexer #(.Bits(32)) multiplexer_60 (
    .sel(register_48_q[1]), .in_0(multiplexer_32_out), .in_1(register_69_q), .out(multiplexer_60_out));
  Multiplexer #(.Bits(8)) multiplexer_61 (
    .sel(register_48_q[1]), .in_0(CT_FU__WR), .in_1(register_70_q), .out(multiplexer_61_out));
  Multiplexer multiplexer_62 (.sel(register_48_q[1]), .in_0(CT_FU__EX), .in_1(register_71_q), .out(multiplexer_62_out));
  and and_105 (MB_MFE, MB_MF, register_49_q);
  and and_106 (MB_st__e, register_49_q, MB_type__st);
  and and_107 (MB_ld__e, register_49_q, ~MB_type__st);  // And
  add_s16c32 add_s16c32_1 (.a(register_54_q), .b(register_55_q), .s(MB_addr));  // open: c
  Multiplexer #(.Bits(32)) multiplexer_63 (.sel(clr), .in_0(addsub_4c32_1_s), .in_1(CT_SC__FD), .out(ISC_sc));
  not not_26 (nand_2_out[0], ALU_busy);
  nand nand_6 (nand_1_out[0], or_41_out, ALU_busy, clr);
  inst_comp inst_comp_8 (.A_id(ALU_A_INST), .A_ep(register_61_q), .B_id(clr_id), .B_ep(clr_ep), .A_new(ALU_A_CMP));
  Multiplexer multiplexer_64 (
    .sel(and_104_out[0]), .in_0(nand_4_out[0]), .in_1(nand_4_out[1]), .out(multiplexer_64_out));
  Multiplexer multiplexer_65 (
    .sel(register_48_q[1]), .in_0(CT_DIR__LD), .in_1(register_72_q[1]), .out(multiplexer_65_out));
  and and_108 (and_108_out, multiplexer_64_out, multiplexer_65_out);
  or or_39 (register_48_q[0], DIR_busy, register_72_q[1], register_48_q[2]);
  nand nand_7 (nand_4_out[1], inst_comp_7_a_new, register_72_q[1], clr);
  Register #(.Bits(4)) register_73 (.D(multiplexer_58_out), .C(C_ct), .en(DIR_LD), .Q(DIR_INST));
  Register register_74 (.D(multiplexer_59_out), .C(C_ct), .en(DIR_LD), .Q(register_74_q));
  Register #(.Bits(32)) register_75 (.D(multiplexer_60_out), .C(C_dt), .en(DIR_LD), .Q(DIR));
  Register #(.Bits(8)) register_76 (.D(multiplexer_61_out), .C(C_ct), .en(DIR_LD), .Q(DIR_WR));
  Register register_77 (.D(multiplexer_62_out), .C(C_ct), .en(DIR_LD), .Q(DIR_EX));
  Register #(.Bits(4)) register_78 (.D(multiplexer_38_out), .C(C_ct), .en(ALU_B_LD), .Q(ALU_B_INST));
  Register register_79 (.D(multiplexer_39_out), .C(C_ct), .en(ALU_B_LD), .Q(register_79_q));
  Register #(.Bits(32)) register_80 (.D(multiplexer_42_out), .C(C_dt), .en(ALU_B_LD), .Q(ALU_B_A));
  Register #(.Bits(32)) register_81 (.D(multiplexer_43_out), .C(C_dt), .en(ALU_B_LD), .Q(ALU_B_B));
  Register #(.Bits(8)) register_82 (.D(multiplexer_44_out), .C(C_dt), .en(ALU_B_LD), .Q(ALU_B_FI));
  Register #(.Bits(9)) register_83 (.D(multiplexer_45_out), .C(C_ct), .en(ALU_B_LD), .Q(ALU_B_CT));
  Register #(.Bits(8)) register_84 (.D(multiplexer_46_out), .C(C_ct), .en(ALU_B_LD), .Q({ALU_B_WR, ALU_B_RM}));
  nand nand_8 (nand_8_out[2], DIR_busy, register_72_q[1], register_48_q[2]);
  and and_109 (LDB_forward, MB_ld__e, LDB_ldV);
  or or_40 (or_40_out, MEM_LD__RD, LDB_forward);
  and and_110 (and_110_out[0], ALU_A_LD, multiplexer_40_out);
  BitExtender #(.inputBits(1), .outputBits(2)) bitextender_6 (.in(ALU_A_CLR), .out(bitextender_6_out));
  and and_111 (and_110_out[1], ALU_A_LD, multiplexer_41_out);
  and and_112 (and_112_out[0], ALU_B_LD, multiplexer_40_out);
  BitExtender #(.inputBits(1), .outputBits(2)) bitextender_7 (.in(ALU_B_CLR), .out(bitextender_7_out));
  and and_113 (and_112_out[1], ALU_B_LD, multiplexer_41_out);
  or or_41 (or_41_out, ALU_A_CMP, ALU_B_CMP);
  nand nand_9 (nand_8_out[1], DIR_busy, register_72_q[1]);
  not not_27 (nand_8_out[0], DIR_busy);
  inst_comp inst_comp_9 (
    .A_id(DIR_INST), .A_ep(register_74_q), .B_id(clr_id), .B_ep(clr_ep), .A_new(inst_comp_9_a_new));
  and and_114 (and_114_out, CT_ISS__OSTB, ~clr);  // And
  Multiplexer #(.Bits(32)) multiplexer_66 (
    .sel(LDB_forward), .in_0(MEM_LD__D), .in_1(LDB_ldD), .out(multiplexer_66_out));
  Multiplexer #(.Bits(4)) multiplexer_67 (
    .sel(LDB_forward), .in_0(MEM_LD__INST), .in_1(MB_INST), .out(multiplexer_67_out));
  and and_115 (and_115_out, CT_ISS__OLDB, ~clr);  // And
  and and_116 (and_116_out, ~and_110_out[0], ALU_A_STD);  // And
  and and_117 (and_117_out, ~and_110_out[1], ALU_A_STF);  // And
  and and_118 (and_118_out, ~and_112_out[0], ALU_B_STD);  // And
  and and_119 (and_119_out, ~and_112_out[1], ALU_B_STF);  // And
  inst_comp inst_comp_10 (.A_id(ALU_B_INST), .A_ep(register_79_q), .B_id(clr_id), .B_ep(clr_ep), .A_new(ALU_B_CMP));
  nand nand_10 (nand_4_out[0], inst_comp_9_a_new, DIR_busy, clr);
  and and_120 (and_120_out, byte_I0[3], byte_I0[0]);
  and and_121 (and_121_out, byte_I0[2], byte_I0[0]);
  and and_122 (and_122_out, byte_I0_iv[3], byte_I0_iv[2], byte_I0[1], byte_I0_iv[0]);
  and and_123 (and_123_out, byte_I0_iv[2], byte_I0_iv[0]);
  and and_124 (and_124_out, byte_I0[2], byte_I0[0]);
  and and_125 (and_125_out, byte_I0[1], byte_I0[2], byte_I0[4]);
  and and_126 (and_126_out, byte_I0[3], byte_I0[4]);
  D_FF #(.Bits(2)) d_ff_9 (.D(and_110_out), .C(C_ct), .Q(d_ff_9_q));  // open: nQ
  assign and_127_out = d_ff_9_q & ~bitextender_6_out;  // And and_127, 2 bits wide
  RS_FF rs_ff_8 (.S(and_110_out[0]), .C(C_ct), .R(and_116_out), .nQ(rs_ff_8_nq));  // open: Q
  RS_FF rs_ff_9 (.S(and_110_out[1]), .C(C_ct), .R(and_117_out), .nQ(rs_ff_9_nq));  // open: Q
  D_FF #(.Bits(2)) d_ff_10 (.D(and_112_out), .C(C_ct), .Q(d_ff_10_q));  // open: nQ
  assign and_128_out = d_ff_10_q & ~bitextender_7_out;  // And and_128, 2 bits wide
  RS_FF rs_ff_10 (.S(and_112_out[0]), .C(C_ct), .R(and_118_out), .nQ(rs_ff_10_nq));  // open: Q
  RS_FF rs_ff_11 (.S(and_112_out[1]), .C(C_ct), .R(and_119_out), .nQ(rs_ff_11_nq));  // open: Q
  and and_129 (and_129_out, ~and_108_out, DIR_ST);  // And
  and and_130 (DIR_CLR, clr, inst_comp_9_a_new);
  store_buffer_debug store_buffer_debug_1 (
    .C(C_dt), .LD(MB_STB__LD), .W_d(MB_st__e), .inst_W(MB_INST), .D(MB_data), .A(MB_addr), .MD(MB_MD),
    .W_id(and_114_out), .epoch(epoch_IS), .inst(inst_IS), .com1(com1), .com2(com2), .com1_id(com1_inst),
    .com2_id(com2_inst), .ld_ep(MB_ep), .ld_id(MB_INST), .ld_addr(MB_addr), .clr(clr), .clr_ep(clr_ep),
    .clr_id(clr_id), .full(store_buffer_debug_1_full), .V(STB_M__V), .D_O(STB_M__D), .A_O(STB_M__A),
    .MD_O(STB_M__MD), .id_O(STB_M__ID), .ep_O(STB_M__EP), .ld_V(LDB_ldV), .ld_D(LDB_ldD));
  load_buffer_debug load_buffer_debug_1 (
    .C(C_dt), .LD(MB_LDB__LD), .LDB(FU_D__V[3]), .W_d(or_40_out), .inst_WD(multiplexer_67_out),
    .D(multiplexer_66_out), .W_a(MB_ld__e), .WC_a(LDB_forward), .inst_WA(MB_INST), .A(MB_addr), .MD(MB_MD),
    .MF(MB_MF), .WR(MB_WR), .PC(MB_PC), .W_id(and_115_out), .epoch(epoch_IS), .inst(inst_IS), .com1(com1),
    .com2(com2), .com1_id(com1_inst), .com2_id(com2_inst), .st(MB_st__e), .st_ep(MB_ep), .st_id(MB_INST),
    .st_addr(MB_addr), .st_data(MB_data), .clr(clr), .clr_ep(clr_ep), .clr_id(clr_id),
    .full(load_buffer_debug_1_full), .V(load_buffer_debug_1_v), .D_O(LDB_B__D),
    .id_O(load_buffer_debug_1_id_o), .WR_O(load_buffer_debug_1_wr_o), .MF_O(load_buffer_debug_1_mf_o),
    .M_V(LDB_M__V), .M_A(LDB_M__A), .M_MD(LDB_M__MD), .M_id(LDB_M__ID), .M_ep(LDB_M__EP), .fl(Fl_MEM),
    .fl_ep(FL_MEM__EP), .fl_id(FL_MEM__ID), .fl_PC(MEM_FPC));
  and and_131 (and_131_out, byte_I0_iv[7], byte_I0_iv[6], byte_I0[5]);
  and and_132 (and_132_out, byte_I0_iv[7], byte_I0[6], byte_I0_iv[5]);
  D_FF #(.Bits(2)) d_ff_11 (.D(and_127_out), .C(C_ct), .Q(d_ff_11_q));  // open: nQ
  and and_133 (ALU_A_UUD, rs_ff_8_nq, ALU_A_V);
  and and_134 (ALU_A_UUF, rs_ff_9_nq, ALU_A_V);
  D_FF #(.Bits(2)) d_ff_12 (.D(and_128_out), .C(C_ct), .Q(d_ff_12_q));  // open: nQ
  and and_135 (ALU_B_UUD, rs_ff_10_nq, ALU_B_V);
  and and_136 (ALU_B_UUF, rs_ff_11_nq, ALU_B_V);
  or or_42 (or_42_out, ALU_A_CLR, and_158_out);
  or or_43 (or_43_out, ALU_B_CLR, and_159_out);
  // alu_32 alu_32_1: pin names not known; wires that end beside it: ALU_A_A, ALU_A_B, ALU_A_FI, ALU_A_CT, ALU_A_RM, alu_32_1_p6, alu_32_1_p6, alu_32_1_p8, alu_32_1_p9, alu_32_1_p9, alu_32_1_p11, alu_32_1_p12, alu_32_1_p12, alu_32_1_p14, ALU_A_R, ALU_A_F
  alu_32 alu_32_2 (
    .A(ALU_B_A), .B(ALU_B_B), .F_I(ALU_B_FI), .CT(ALU_B_CT), .RM(ALU_B_RM), .E_A(alu_32_1_p8),
    .E_B(alu_32_1_p11), .E(alu_32_1_p14), .R_O(ALU_B_R), .F_O(ALU_B_F));
  RS_FF rs_ff_12 (.S(and_108_out), .C(C_ct), .R(and_129_out), .nQ(rs_ff_12_nq));  // open: Q
  D_FF V (.D(DIR_LD), .C(C_ct), .Q(V_q));  // open: nQ
  bus16x2_demux bus16x2_demux_3 (.bus_1(V1_inst), .bus_2(V2_inst), .E(DIR_V), .id(DIR_INST));
  and and_137 (and_137_out, byte_I0[4], byte_I0[3], byte_I0_iv[1], byte_I0_iv[2], byte_I0_iv[5], byte_I0_iv[6], byte_I0_iv[7]);
  or or_44 (or_44_out, and_120_out, and_121_out, and_122_out);
  nor nor_8 (nor_8_out, byte_I0[3], byte_I0[1], and_123_out, and_124_out);
  nor nor_9 (nor_9_out, and_125_out, and_126_out);
  and and_138 (and_138_out, byte_I0_iv[0], byte_I0_iv[1], byte_I0[2], byte_I0[3], byte_I0[4], byte_I0_iv[5], byte_I0_iv[6], byte_I0_iv[7]);
  and and_139 (and_139_out, byte_I0[1], byte_I0_iv[2], byte_I0[3], byte_I0[4], byte_I0_iv[5], byte_I0_iv[6], byte_I0_iv[7]);
  and and_140 (and_140_out, byte_I0_iv[4], byte_I0[5], byte_I0[6], byte_I0_iv[7]);
  and and_141 (and_141_out, com1, CT_FL__W1);
  and and_142 (and_142_out, com2, CT_FL__W2);
  assign {ALU_A_FRE, ALU_A_DRE} = d_ff_11_q & ~bitextender_6_out;  // And and_143, 2 bits wide
  assign {ALU_B_FRE, ALU_B_DRE} = d_ff_12_q & ~bitextender_7_out;  // And and_144, 2 bits wide
  and and_145 (and_145_out, ALU_A_VD, ~or_42_out);  // And
  and and_146 (and_146_out, ALU_A_VF, ~or_42_out);  // And
  and and_147 (and_147_out, ALU_B_VD, ~or_43_out);  // And
  and and_148 (and_148_out, ALU_B_VF, ~or_43_out);  // And
  PullDown #(.Bits(32)) pulldown_24 (.out(alu_32_1_p12));
  PullDown #(.Bits(32)) pulldown_25 (.out(alu_32_1_p14));
  or or_45 (DIR_free, DIR_ST, rs_ff_12_nq);
  and and_149 (DIR_RD, V_q, ~DIR_CLR);  // And
  D_FF d_ff_13 (.D(store_buffer_debug_1_full), .C(C_ct), .Q(STB_busy));  // open: nQ
  D_FF d_ff_14 (.D(load_buffer_debug_1_full), .C(C_ct), .Q(LDB_busy));  // open: nQ
  D_FF #(.Bits(4)) d_ff_15 (.D(load_buffer_debug_1_id_o), .C(C_ct), .Q(LDB_B__INST));  // open: nQ
  D_FF d_ff_16 (.D(load_buffer_debug_1_mf_o), .C(C_ct), .Q(LDB_B__MF));  // open: nQ
  and and_150 (and_150_out, byte_I0[1], byte_I0[2], byte_I0[3], byte_I0[4], byte_I0_iv[5], byte_I0_iv[6], byte_I0_iv[7]);
  or or_46 (or_46_out, and_131_out, and_132_out);
  Comparator #(.Bits(3)) comparator_19 (.a(byte_I0[2:0]), .b(3'b110), .eq(comparator_19_eq));  // open: gt, lt
  or or_47 (CT_RF__FLS, and_141_out, and_142_out);
  RS_FF rs_ff_13 (.S(ALU_A_DRE), .C(C_ct), .R(ALU_A_DRD), .Q(ALU_A_DRD));  // open: nQ
  RS_FF rs_ff_14 (.S(ALU_A_FRE), .C(C_ct), .R(ALU_A_FRD), .Q(ALU_A_FRD));  // open: nQ
  RS_FF rs_ff_15 (.S(ALU_B_DRE), .C(C_ct), .R(ALU_B_DRD), .Q(ALU_B_DRD));  // open: nQ
  RS_FF rs_ff_16 (.S(ALU_B_FRE), .C(C_ct), .R(ALU_B_FRD), .Q(ALU_B_FRD));  // open: nQ
  RS_FF rs_ff_17 (.S(and_145_out), .C(C_ct), .R(or_42_out), .Q(rs_ff_17_q));  // open: nQ
  RS_FF rs_ff_18 (.S(and_146_out), .C(C_ct), .R(or_42_out), .Q(rs_ff_18_q));  // open: nQ
  RS_FF rs_ff_19 (.S(and_147_out), .C(C_ct), .R(or_43_out), .Q(rs_ff_19_q));  // open: nQ
  RS_FF rs_ff_20 (.S(and_148_out), .C(C_ct), .R(or_43_out), .Q(rs_ff_20_q));  // open: nQ
  D_FF #(.Bits(8)) d_ff_17 (.D(load_buffer_debug_1_wr_o), .C(C_ct), .Q(LDB_B__WR));  // open: nQ
  and and_151 (and_151_out, byte_I0_iv[7], byte_I0_iv[6], byte_I0_iv[5], byte_I0_iv[4]);
  and and_152 (and_152_out, byte_I0_iv[7], byte_I0_iv[6], byte_I0_iv[5], byte_I0[4], byte_I0_iv[3]);
  or or_48 (or_48_out, and_138_out, and_139_out);
  and and_153 (and_153_out, byte_I0[0], byte_I0_iv[1], byte_I0[2], byte_I0[3], byte_I0[4], byte_I0_iv[5], byte_I0_iv[6], byte_I0_iv[7]);
  not not_28 (not_28_out, comparator_19_eq);
  or or_49 (or_49_out, ALU_A_VD, ALU_A_UUD, rs_ff_17_q);
  or or_50 (or_50_out, ALU_A_VF, ALU_A_UUF, rs_ff_18_q);
  or or_51 (or_51_out, ALU_B_VD, ALU_B_UUD, rs_ff_19_q);
  or or_52 (or_52_out, ALU_B_VF, ALU_B_UUF, rs_ff_20_q);
  and and_154 (DIR_LD, and_108_out, DIR_free);
  not not_29 (DIR_busy, DIR_free);
  and and_155 (and_155_out, d_ff_18_q, ~FU_D__V[3]);  // And
  not not_30 (not_30_out, or_44_out);
  and and_156 (and_156_out, and_150_out, byte_I0[0]);
  and and_157 (and_157_out, byte_I0_iv[0], and_150_out);
  or or_53 (or_53_out, ALU_A_STD, rs_ff_8_nq);
  or or_54 (or_54_out, ALU_A_STF, rs_ff_9_nq);
  or or_55 (or_55_out, ALU_B_STD, rs_ff_10_nq);
  or or_56 (or_56_out, ALU_B_STF, rs_ff_11_nq);
  and and_158 (and_158_out, or_49_out, ~ALU_A_CLR, or_50_out);  // And
  bus16x2_demux bus16x2_demux_4 (.bus_1(V1_inst), .bus_2(V2_inst), .E(and_158_out), .id(ALU_A_INST));
  and and_159 (and_159_out, or_51_out, ~ALU_B_CLR, or_52_out);  // And
  bus16x2_demux bus16x2_demux_5 (.bus_1(V1_inst), .bus_2(V2_inst), .E(and_159_out), .id(ALU_B_INST));
  nor nor_10 (ALU_busy, ALU_A_LRD, ALU_B_LRD);
  or or_57 (ALU_free, ALU_A_LRD, ALU_B_LRD);
  Register #(.Bits(32)) register_85 (.D(ALU_A_R), .C(C_dt), .en(ALU_A_DRE), .Q(ALU_A_T__R));
  Register #(.Bits(8)) register_86 (.D(ALU_A_F), .C(C_dt), .en(ALU_A_FRE), .Q(ALU_A_T__F));
  Register #(.Bits(32)) register_87 (.D(ALU_B_R), .C(C_dt), .en(ALU_B_DRE), .Q(ALU_B_T__R));
  Register #(.Bits(8)) register_88 (.D(ALU_B_F), .C(C_dt), .en(ALU_B_FRE), .Q(ALU_B_T__F));
  and and_160 (and_160_out, ~MB_MF, MB_st__e);  // And
  and and_161 (and_161_out, ~LDB_B__MF, FU_D__V[3]);  // And
  D_FF d_ff_18 (.D(load_buffer_debug_1_v), .C(C_ct), .Q(d_ff_18_q));  // open: nQ
  D_FF d_ff_19 (.D(and_155_out), .C(C_ct), .nQ(d_ff_19_nq));  // open: Q
  and and_162 (LDB_B__RD, d_ff_18_q, d_ff_19_nq);
  or or_58 (or_58_out, and_151_out, and_137_out, and_152_out);
  assign issue = or_58_out ? issue_e : 1'bz;  // Driver driver_125
  assign CT_ISS__URA = or_58_out ? 1'b1 : 1'bz;  // Driver driver_126
  assign CT_ISS__URB = or_58_out ? not_30_out : 1'bz;  // Driver driver_127
  assign CT_ISS__RA = or_58_out ? byte_I1[7:3] : 5'bz;  // Driver driver_128
  assign CT_ISS__RB = or_58_out ? byte_I2[7:3] : 5'bz;  // Driver driver_129
  assign CT_ISS__UFL = or_58_out ? nor_8_out : 1'bz;  // Driver driver_130
  assign CT_ISS__ORC = or_58_out ? nor_9_out : 1'bz;  // Driver driver_131
  assign CT_ISS__RC = or_58_out ? byte_I1[7:3] : 5'bz;  // Driver driver_132
  assign CT_ISS__OFL = or_58_out ? 1'b1 : 1'bz;  // Driver driver_133
  assign CT_ISS__UFU = or_58_out ? 3'b001 : 3'bz;  // Driver driver_134
  assign CT_ISS__URA = and_138_out ? 1'b1 : 1'bz;  // Driver driver_135
  assign CT_ISS__RA = and_138_out ? byte_I2[7:3] : 5'bz;  // Driver driver_136
  assign issue = or_48_out ? issue_e : 1'bz;  // Driver driver_137
  assign CT_ISS__ORC = or_48_out ? 1'b1 : 1'bz;  // Driver driver_138
  assign CT_ISS__RC = or_48_out ? byte_I1[7:3] : 5'bz;  // Driver driver_139
  assign CT_ISS__UFU = or_48_out ? 3'b010 : 3'bz;  // Driver driver_140
  assign issue = and_150_out ? issue_e : 1'bz;  // Driver driver_141
  assign CT_ISS__URB = and_150_out ? 1'b1 : 1'bz;  // Driver driver_142
  assign CT_ISS__RB = and_150_out ? 5'b11110 : 5'bz;  // Driver driver_143
  assign CT_ISS__OSC = and_150_out ? 1'b1 : 1'bz;  // Driver driver_144
  assign CT_ISS__UMM = and_150_out ? 1'b1 : 1'bz;  // Driver driver_145
  assign CT_ISS__UFU = and_150_out ? 3'b011 : 3'bz;  // Driver driver_146
  assign CT_ISS__URA = and_156_out ? 1'b1 : 1'bz;  // Driver driver_147
  assign CT_ISS__RA = and_156_out ? byte_I1[7:3] : 5'bz;  // Driver driver_148
  assign CT_ISS__OSTB = and_156_out ? issue_e : 1'bz;  // Driver driver_149
  assign CT_ISS__ORC = and_157_out ? 1'b1 : 1'bz;  // Driver driver_150
  assign CT_ISS__RC = and_157_out ? byte_I1[7:3] : 5'bz;  // Driver driver_151
  assign CT_ISS__OLDB = and_157_out ? issue_e : 1'bz;  // Driver driver_152
  assign issue = or_46_out ? issue_e : 1'bz;  // Driver driver_153
  assign CT_ISS__URA = or_46_out ? 1'b1 : 1'bz;  // Driver driver_154
  assign CT_ISS__RA = or_46_out ? byte_I0[4:0] : 5'bz;  // Driver driver_155
  assign CT_ISS__UMM = or_46_out ? 1'b1 : 1'bz;  // Driver driver_156
  assign CT_ISS__UFU = or_46_out ? 3'b011 : 3'bz;  // Driver driver_157
  assign CT_ISS__URB = and_132_out ? 1'b1 : 1'bz;  // Driver driver_158
  assign CT_ISS__RB = and_132_out ? byte_I1[7:3] : 5'bz;  // Driver driver_159
  assign CT_ISS__ORC = and_131_out ? 1'b1 : 1'bz;  // Driver driver_160
  assign CT_ISS__RC = and_131_out ? byte_I1[7:3] : 5'bz;  // Driver driver_161
  assign CT_ISS__OLDB = and_131_out ? issue_e : 1'bz;  // Driver driver_162
  assign CT_ISS__OSTB = and_132_out ? issue_e : 1'bz;  // Driver driver_163
  assign issue = and_153_out ? issue_e : 1'bz;  // Driver driver_164
  assign CT_BLOCK = and_153_out ? 1'b1 : 1'bz;  // Driver driver_165
  assign CT_UBTB = and_140_out ? issue_e : 1'bz;  // Driver driver_166
  assign issue = and_140_out ? issue_e : 1'bz;  // Driver driver_167
  assign CT_ISS__URA = and_140_out ? 1'b1 : 1'bz;  // Driver driver_168
  assign CT_ISS__RA = and_140_out ? byte_I1[7:3] : 5'bz;  // Driver driver_169
  assign CT_ISS__UFL = and_140_out ? not_28_out : 1'bz;  // Driver driver_170
  assign CT_ISS__UFU = and_140_out ? 3'b111 : 3'bz;  // Driver driver_171
  DipSwitch dipswitch_15 (.out(MB_busy));
  Multiplexer #(.Bits(8)) multiplexer_68 (.sel(and_142_out), .in_0(CT_FL__D1), .in_1(CT_FL__D2), .out(fl_i));
  and and_163 (ALU_A_LD, and_102_out, or_54_out, or_53_out);
  and and_164 (ALU_A_LRD, or_53_out, or_54_out);
  nand nand_11 (nand_11_out, or_53_out, or_54_out);
  and and_165 (ALU_B_LD, nand_11_out, and_102_out, or_56_out, or_55_out);
  and and_166 (ALU_B_LRD, or_55_out, or_56_out);
  and and_167 (and_167_out, ~ALU_A_LD, or_42_out);  // And
  and and_168 (and_168_out, ~ALU_B_LD, or_43_out);  // And
  bus16_demux bus16_demux_1 (.bus(V1_inst), .E(MB_st__e), .id(MB_INST));
  bus16_demux bus16_demux_2 (.bus(V2_inst), .E(and_160_out), .id(MB_INST));
  bus16_demux bus16_demux_3 (.bus(V1_inst), .E(FU_D__V[3]), .id(LDB_B__INST));
  bus16_demux bus16_demux_4 (.bus(V2_inst), .E(and_161_out), .id(LDB_B__INST));
  not not_31 (MB_free, MB_busy);
  and and_169 (ALU_A_CLR, clr, ALU_A_CMP);
  and and_170 (ALU_B_CLR, clr, ALU_B_CMP);
  RS_FF rs_ff_21 (.S(ALU_A_LD), .C(C_ct), .R(and_167_out), .Q(ALU_A_V));  // open: nQ
  RS_FF rs_ff_22 (.S(ALU_B_LD), .C(C_ct), .R(and_168_out), .Q(ALU_B_V));  // open: nQ
  and and_171 (and_171_out, byte_I0[1], byte_I0_iv[2], byte_I0[3], byte_I0[4], byte_I0[5], byte_I0[6], byte_I0_iv[7]);
  not not_32 (not_32_out, E_t);
  and and_172 (and_172_out, byte_I0_iv[0], byte_I0_iv[1], byte_I0_iv[2], byte_I0_iv[3], byte_I0[4], byte_I0[5], byte_I0[6], byte_I0_iv[7]);
  and and_173 (and_173_out, byte_I0[0], byte_I0_iv[1], byte_I0_iv[2], byte_I0_iv[3], byte_I0[4], byte_I0[5], byte_I0[6], byte_I0_iv[7]);
  and and_174 (and_174_out, byte_I0_iv[1], byte_I0[2], byte_I0_iv[3], byte_I0[4], byte_I0[5], byte_I0[6], byte_I0_iv[7]);
  and and_175 (and_175_out, byte_I0[0], and_171_out);
  and and_176 (and_176_out, and_171_out, byte_I0_iv[0]);
  and and_177 (and_177_out, byte_I0_iv[0], byte_I0[1], byte_I0[2], byte_I0_iv[3], byte_I0[4], byte_I0[5], byte_I0[6], byte_I0_iv[7]);
  res_station_debug res_station_debug_1 (
    .C(C_ct), .res(not_32_out), .E(issue), .D({byte_I0, byte_I1, byte_I2, byte_I3}), .BTB_PK(BTB_pack__iss),
    .ep_I(epoch_IS), .inst(inst_IS), .URA(CT_ISS__URA), .URB(CT_ISS__URB), .RA(CT_ISS__RA), .RB(CT_ISS__RB),
    .UMM(CT_ISS__UMM), .UFL(CT_ISS__UFL), .UFU(CT_ISS__UFU), .ORC(CT_ISS__ORC), .RC(CT_ISS__RC),
    .OSC(CT_ISS__OSC), .OFL(CT_ISS__OFL), .BLOCK(CT_BLOCK), .com1(com1), .com2(com2), .com1_inst(com1_inst),
    .com2_inst(com2_inst), .clr(clr), .clr_ep(clr_ep), .clr_id(clr_id), .FU_free(FU_free), .V(CT_DISP),
    .disp_32({res_station_debug_1_disp_32, byte_D1, byte_D2, byte_D3}), .BTB_DP(BTB_DP), .ep_O(epoch_DP),
    .disp(inst_DP), .full(RS_full));
  store_controller store_controller_1 (
    .C(C_ct), .in1(ALU_A_DRD), .in2(ALU_B_DRD), .in3(DIR_RD), .in4(LDB_B__RD), .in5(1'b0), .in6(1'b0),
    .in7(1'b0), .in8(1'b0), .clr({3'b000, FU_CLR[4], 1'b0, DIR_CLR, ALU_B_CLR, ALU_A_CLR}),
    .D1_sel(store_controller_1_d1_sel), .D2_sel(store_controller_1_d2_sel), .ST1(CT_ROB__GEN__STA),
    .ST2(CT_ROB__GEN__STB), .out1(ALU_A_STD), .out2(ALU_B_STD), .out3(DIR_ST), .out4(LDB_B__ST),
    .V({FU_D__V, DIR_V, ALU_B_VD, ALU_A_VD}));  // open: out5, out6, out7, out8
  store_controller_half store_controller_half_1 (
    .C(C_ct), .in1(ALU_A_FRD), .in2(ALU_B_FRD), .in3(1'b0), .in4(1'b0),
    .clr({1'b0, DIR_CLR, ALU_B_CLR, ALU_A_CLR}), .D1_sel(store_controller_half_1_d1_sel),
    .D2_sel(store_controller_half_1_d2_sel), .ST1(CT_ROB__FL__STA), .ST2(CT_ROB__FL__STB), .out1(ALU_A_STF),
    .out2(ALU_B_STF), .V({FU_F__V, ALU_B_VF, ALU_A_VF}));  // open: out3, out4
  store_controller_half store_controller_half_2 (
    .C(C_ct), .in1(TRAP_IRD), .in2(1'b0), .in3(1'b0), .in4(1'b0), .clr({3'b000, FU_CLR[4]}),
    .D1_sel(store_controller_half_2_d1_sel), .D2_sel(store_controller_half_2_d2_sel), .ST1(CT_ROB__INT__STA),
    .ST2(CT_ROB__INT__STB), .out1(TRAP_ST), .V(FU_I__V));  // open: out2, out3, out4
  Demultiplexer #(.Selector_Bits(4)) demultiplexer_3 (
    .sel(priorityencoder_1_num), .in(and_188_out), .out_0(demultiplexer_3_out_0[0]),
    .out_1(demultiplexer_3_out_0[1]), .out_2(demultiplexer_3_out_0[2]), .out_3(demultiplexer_3_out_0[3]),
    .out_4(demultiplexer_3_out_0[4]), .out_5(demultiplexer_3_out_0[5]), .out_6(demultiplexer_3_out_0[6]),
    .out_7(demultiplexer_3_out_0[7]), .out_8(demultiplexer_3_out_0[8]), .out_9(demultiplexer_3_out_0[9]),
    .out_10(demultiplexer_3_out_0[10]), .out_11(demultiplexer_3_out_0[11]),
    .out_12(demultiplexer_3_out_0[12]), .out_13(demultiplexer_3_out_0[13]),
    .out_14(demultiplexer_3_out_0[14]), .out_15(demultiplexer_3_out_0[15]));
  Demultiplexer #(.Selector_Bits(4)) demultiplexer_4 (
    .sel(CT_FU__INST), .in(CT_RET__LD), .out_0(demultiplexer_4_out_0[0]), .out_1(demultiplexer_4_out_0[1]),
    .out_2(demultiplexer_4_out_0[2]), .out_3(demultiplexer_4_out_0[3]), .out_4(demultiplexer_4_out_0[4]),
    .out_5(demultiplexer_4_out_0[5]), .out_6(demultiplexer_4_out_0[6]), .out_7(demultiplexer_4_out_0[7]),
    .out_8(demultiplexer_4_out_0[8]), .out_9(demultiplexer_4_out_0[9]), .out_10(demultiplexer_4_out_0[10]),
    .out_11(demultiplexer_4_out_0[11]), .out_12(demultiplexer_4_out_0[12]),
    .out_13(demultiplexer_4_out_0[13]), .out_14(demultiplexer_4_out_0[14]), .out_15(demultiplexer_4_out_0[15]));
  or or_59 (or_59_out, JPU_INT, JPU_RET);
  nor nor_11 (nor_11_out, JPU_INT, JPU_RET);
  nor nor_12 (nor_12_out, JPU_INT, JPU_RET);
  assign ISS_kernel = and_174_out ? byte_I0[0] : 1'bz;  // Driver driver_172
  assign CT_BLOCK = and_174_out ? 1'b1 : 1'bz;  // Driver driver_173
  assign issue = and_174_out ? issue_e : 1'bz;  // Driver driver_174
  assign CT_ISS__HALT = and_174_out ? 1'b1 : 1'bz;  // Driver driver_175
  assign CT_ISS__UMM = and_174_out ? 1'b1 : 1'bz;  // Driver driver_176
  assign CT_ISS__UFU = and_174_out ? 3'b100 : 3'bz;  // Driver driver_177
  assign CT_ISS__URA = and_175_out ? 1'b1 : 1'bz;  // Driver driver_178
  assign CT_ISS__RA = and_175_out ? byte_I1[7:3] : 5'bz;  // Driver driver_179
  assign ISS_kernel = and_171_out ? 1'b1 : 1'bz;  // Driver driver_180
  assign issue = and_171_out ? issue_e : 1'bz;  // Driver driver_181
  assign CT_ISS__UFU = and_171_out ? 3'b010 : 3'bz;  // Driver driver_182
  assign CT_ISS__ORC = and_176_out ? 1'b1 : 1'bz;  // Driver driver_183
  assign CT_ISS__RC = and_176_out ? byte_I1[7:3] : 5'bz;  // Driver driver_184
  assign CT_BLOCK = and_177_out ? 1'b1 : 1'bz;  // Driver driver_185
  assign issue = and_177_out ? issue_e : 1'bz;  // Driver driver_186
  assign CT_ISS__HALT = and_177_out ? 1'b1 : 1'bz;  // Driver driver_187
  assign CT_ISS__UMM = and_177_out ? 1'b1 : 1'bz;  // Driver driver_188
  assign CT_ISS__UFU = and_177_out ? 3'b100 : 3'bz;  // Driver driver_189
  PullDown #(.Bits(3)) pulldown_26 (.out(CT_ISS__UFU));
  PullDown pulldown_27 (.out(CT_ISS__OSTB));
  PullDown pulldown_28 (.out(clr));
  PullDown pulldown_29 (.out(clr_ep));
  PullDown #(.Bits(4)) pulldown_30 (.out(clr_id));
  Multiplexer #(.Bits(32)) multiplexer_69 (.sel(JPU_INT), .in_0(CT_RF__DR), .in_1(int_vec_t), .out(multiplexer_69_out));
  BitExtender #(.inputBits(1)) bitextender_8 (.in(nor_11_out), .out(bitextender_8_out));
  BitExtender #(.inputBits(1), .outputBits(37)) bitextender_9 (.in(nor_12_out), .out(bitextender_9_out));
  BitExtender #(.inputBits(1)) bitextender_10 (.in(CT_FU__EPOCH), .out(bitextender_10_out));
  assign not_33_out = ~demultiplexer_4_out_0;  // Not not_33, 16 bits wide
  BitExtender #(.inputBits(1)) bitextender_11 (.in(CT_FU__EPOCH), .out(bitextender_11_out));
  assign issue = and_172_out ? issue_e : 1'bz;  // Driver driver_190
  assign CT_ISS__URA = and_172_out ? 1'b1 : 1'bz;  // Driver driver_191
  assign CT_ISS__RA = and_172_out ? byte_I1[7:3] : 5'bz;  // Driver driver_192
  assign CT_ISS__URB = and_172_out ? 1'b1 : 1'bz;  // Driver driver_193
  assign CT_ISS__RB = and_172_out ? 5'b11110 : 5'bz;  // Driver driver_194
  assign CT_ISS__OSC = and_172_out ? 1'b1 : 1'bz;  // Driver driver_195
  assign CT_ISS__UMM = and_172_out ? 1'b1 : 1'bz;  // Driver driver_196
  assign CT_ISS__UFU = and_172_out ? 3'b110 : 3'bz;  // Driver driver_197
  assign CT_ISS__OSTB = and_172_out ? issue_e : 1'bz;  // Driver driver_198
  assign CT_UBTB = and_172_out ? issue_e : 1'bz;  // Driver driver_199
  assign issue = and_173_out ? issue_e : 1'bz;  // Driver driver_200
  assign CT_ISS__URB = and_173_out ? 1'b1 : 1'bz;  // Driver driver_201
  assign CT_ISS__RB = and_173_out ? 5'b11110 : 5'bz;  // Driver driver_202
  assign CT_ISS__OSC = and_173_out ? 1'b1 : 1'bz;  // Driver driver_203
  assign CT_ISS__UMM = and_173_out ? 1'b1 : 1'bz;  // Driver driver_204
  assign CT_ISS__UFU = and_173_out ? 3'b110 : 3'bz;  // Driver driver_205
  assign CT_ISS__OLDB = and_173_out ? issue_e : 1'bz;  // Driver driver_206
  assign CT_UBTB = and_173_out ? issue_e : 1'bz;  // Driver driver_207
  Multiplexer #(.Bits(8)) multiplexer_70 (
    .sel(CT_DISP), .in_0(8'h72), .in_1(res_station_debug_1_disp_32), .out(byte_D0));
  Multiplexer #(.Bits(32)) multiplexer_71 (.sel(JPU_RET), .in_0(pc_read), .in_1(pc_ret__int), .out(multiplexer_71_out));
  Multiplexer #(.Bits(4)) multiplexer_72 (.sel(JPU_RET), .in_0(CT_FU__INST), .in_1(RET_INST), .out(multiplexer_72_out));
  Multiplexer multiplexer_73 (.sel(JPU_RET), .in_0(CT_FU__EPOCH), .in_1(RET_EPOCH), .out(multiplexer_73_out));
  Multiplexer #(.Bits(32)) multiplexer_74 (
    .sel(or_59_out), .in_0(R_A), .in_1(multiplexer_69_out), .out(multiplexer_74_out));
  assign and_178_out = {byte_D2, byte_D3} & bitextender_8_out;  // And and_178, 16 bits wide
  assign and_179_out = BTB_DP & bitextender_9_out;  // And and_179, 37 bits wide
  or or_60 (or_60_out, CT_JPU__JP, JPU_INT, JPU_RET);
  or or_61 (or_61_out, CT_FU__MF, JPU_RET);
  assign not_34_out = ~demultiplexer_3_out_0;  // Not not_34, 16 bits wide
  assign or_62_out = bitextender_10_out | not_33_out;  // Or or_62, 16 bits wide
  assign and_180_out = bitextender_11_out & demultiplexer_4_out_0;  // And and_180, 16 bits wide
  and and_181 (and_181_out, ~CT_JPU__LD, JPU_BTB__ST);  // And
  assign or_63_out = register_97_q | demultiplexer_4_out_0;  // Or or_63, 16 bits wide
  assign or_64_out = register_98_q | and_180_out;  // Or or_64, 16 bits wide
  // data_select_32 data_select_32_1: pin names not known; wires that end beside it: store_controller_1_d1_sel, store_controller_1_d2_sel, ALU_A_T__R, ALU_B_T__R, DIR, LDB_B__D, {32{1'b0}}, {32{1'b0}}, {32{1'b0}}, {32{1'b0}}, ROB_GEN_DA, ROB_GEN_DB
  data_select_8H data_select_8h_1 (
    .D1_sel(store_controller_half_1_d1_sel), .D2_sel(store_controller_half_1_d2_sel), .in1(ALU_A_T__F),
    .in2(ALU_B_T__F), .in3({8{1'b0}}), .in4({8{1'b0}}), .out1(ROB_FL_A), .out2(ROB_FL_B));
  data_select_6H data_select_6h_1 (
    .D1_sel(store_controller_half_2_d1_sel), .D2_sel(store_controller_half_2_d2_sel), .in1(TRAP_INT),
    .in2({6{1'b0}}), .in3({6{1'b0}}), .in4({6{1'b0}}), .out1(ROB_INT_A), .out2(ROB_INT_B));
  RS_FF rs_ff_23 (.S(CT_JPU__LD), .C(C_ct), .R(and_181_out), .Q(JPU_BTB__ST), .nQ(rs_ff_23_nq));
  Register #(.Bits(32)) register_89 (.D(multiplexer_71_out), .C(C_dt), .en(JPU_LD), .Q(JPU_PC));
  Register #(.Bits(4)) register_90 (.D(multiplexer_72_out), .C(C_ct), .en(JPU_LD), .Q(Fl_JPU__INST));
  Register register_91 (.D(multiplexer_73_out), .C(C_ct), .en(JPU_LD), .Q(Fl_JPU__EP));
  Register #(.Bits(32)) register_92 (.D(multiplexer_74_out), .C(C_dt), .en(JPU_LD), .Q(register_92_q));
  Register #(.Bits(16)) register_93 (.D(and_178_out), .C(C_dt), .en(JPU_LD), .Q(register_93_q));
  Register #(.Bits(37)) register_94 (
    .D(and_179_out), .C(C_ct), .en(JPU_LD),
    .Q({JPU_BTB__tar, JPU_BTB__pred, JPU_BTB__J, JPU_BTB__V, JPU_BTBPK[0]}));
  Register register_95 (.D(or_60_out), .C(C_ct), .en(JPU_LD), .Q(JPU_JP));
  Register register_96 (.D(or_61_out), .C(C_ct), .en(JPU_LD), .Q(JPU_MF));
  assign and_182_out = icmks_16 & not_34_out & or_63_out;  // And and_182, 16 bits wide
  or or_65 (or_65_out, CT_RET__LD, and_188_out, ext_en);
  assign and_183_out = or_62_out & or_64_out;  // And and_183, 16 bits wide
  or or_66 (or_66_out, rs_ff_23_nq, JPU_BTB__ST);
  D_FF #(.Bits(32)) d_ff_20 (.D(register_92_q), .C(C_ct), .Q(d_ff_20_q));  // open: nQ
  D_FF #(.Bits(16)) d_ff_21 (.D(register_93_q), .C(C_ct), .Q(d_ff_21_q));  // open: nQ
  and and_184 (JPU_LD, CT_JPU__LD, or_66_out);
  Register #(.Bits(16)) register_97 (.D(and_182_out), .C(C_ct), .en(or_65_out), .Q(register_97_q));
  Register #(.Bits(16)) register_98 (.D(and_183_out), .C(C_ct), .en(or_65_out), .Q(register_98_q));
  add_s16c32 add_s16c32_2 (.a(multiplexer_75_out), .b(multiplexer_76_out), .s(JPU_ADDR));  // open: c
  Multiplexer #(.Bits(32)) multiplexer_75 (.sel(JPU_JP), .in_0(JPU_PC), .in_1(d_ff_20_q), .out(multiplexer_75_out));
  Multiplexer #(.Bits(16)) multiplexer_76 (.sel(JPU_JP), .in_0(16'h4), .in_1(d_ff_21_q), .out(multiplexer_76_out));
  assign and_185_out = V1_inst & register_97_q;  // And and_185, 16 bits wide
  BitSelector #(.Selector_Bits(4)) bitselector_1 (
    .in(register_98_q), .sel(priorityencoder_1_num), .out(bitselector_1_out));
  PullDown pulldown_31 (.out(CT_ALU__M));
  PullDown pulldown_32 (.out(CT_ALU__LD));
  PullDown pulldown_33 (.out(CT_ALU__WD));
  PullDown pulldown_34 (.out(CT_ALU__WF));
  PullDown pulldown_35 (.out(CT_FU__EPOCH));
  PullDown #(.Bits(4)) pulldown_36 (.out(CT_FU__INST));
  PullDown #(.Bits(8)) pulldown_37 (.out(CT_FU__WR));
  PullDown pulldown_38 (.out(CT_DIR__LD));
  PullDown pulldown_39 (.out(CT_DIR__M));
  PullDown pulldown_40 (.out(CT_DIR__MS));
  PullDown pulldown_41 (.out(MB_ep));
  PullDown #(.Bits(4)) pulldown_42 (.out(LD_id));
  PullDown #(.Bits(32)) pulldown_43 (.out(LD_addr));
  PullDown pulldown_44 (.out(CT_STB__LD));
  PullDown pulldown_45 (.out(CT_LDB__LD));
  PullDown pulldown_46 (.out(CT_MB__LD));
  PullDown pulldown_47 (.out(CT_MB__ST));
  PullDown pulldown_48 (.out(CT_ISS__OLDB));
  PullDown pulldown_49 (.out(CT_UBTB));
  PullDown pulldown_50 (.out(CT_USCB));
  and and_186 (and_186_out, ~JPU_MF, JPU_BTB__ST);  // And
  data_select_8 data_select_8_1 (
    .D1_sel(store_controller_1_d1_sel), .D2_sel(store_controller_1_d2_sel), .in1({ALU_A_WR, ALU_A_RM}),
    .in2({ALU_B_WR, ALU_B_RM}), .in3(DIR_WR), .in4(LDB_B__WR), .in5({8{1'b0}}), .in6({8{1'b0}}),
    .in7({8{1'b0}}), .in8({8{1'b0}}), .out1(ROB_GEN_WA), .out2(ROB_GEN_WB));
  data_select_4H data_select_4h_1 (
    .D1_sel(store_controller_half_1_d1_sel), .D2_sel(store_controller_half_1_d2_sel), .in1(ALU_A_INST),
    .in2(ALU_B_INST), .in3(4'b0000), .in4(4'b0000), .out1(ROB_FL_INSTA), .out2(ROB_FL_INSTB));
  data_select_4H data_select_4h_2 (
    .D1_sel(store_controller_half_2_d1_sel), .D2_sel(store_controller_half_2_d2_sel), .in1(TRAP_INST),
    .in2(4'b0000), .in3(4'b0000), .in4(4'b0000), .out1(ROB_INT_INSTA), .out2(ROB_INT_INSTB));
  PriorityEncoder #(.Selector_Bits(4)) priorityencoder_1 (
    .in0(and_185_out[0]), .in1(and_185_out[1]), .in2(and_185_out[2]), .in3(and_185_out[3]),
    .in4(and_185_out[4]), .in5(and_185_out[5]), .in6(and_185_out[6]), .in7(and_185_out[7]),
    .in8(and_185_out[8]), .in9(and_185_out[9]), .in10(and_185_out[10]), .in11(and_185_out[11]),
    .in12(and_185_out[12]), .in13(and_185_out[13]), .in14(and_185_out[14]), .in15(and_185_out[15]),
    .num(priorityencoder_1_num), .any(priorityencoder_1_any));
  PullDown pulldown_51 (.out(CT_BLOCK));
  and and_187 (JPU_MFE, JPU_MF, JPU_BTB__ST);
  bus16_demux bus16_demux_5 (.bus(V1_inst), .E(and_186_out), .id(Fl_JPU__INST));
  bus16_demux bus16_demux_6 (.bus(V2_inst), .E(JPU_BTB__ST), .id(Fl_JPU__INST));
  not not_35 (not_35_out, BTB_override);
  and and_188 (and_188_out, FU_D__V[3], priorityencoder_1_any);
  xor xor_8 (JPU_MISS, JPU_BTB__J, JPU_JP);
  not not_36 (not_36_out, JPU_BTB__pred[0]);
  PullDown pulldown_52 (.out(kernel_inst));
  PullDown pulldown_53 (.out(CT_RF__E));
  PullDown pulldown_54 (.out(CT_RF__DM));
  PullDown #(.Bits(5)) pulldown_55 (.out(CT_RF__WS));
  PullDown #(.Bits(3)) pulldown_56 (.out(CT_RF__WM));
  PullDown #(.Bits(5)) pulldown_57 (.out(CT_RF__RA));
  PullDown #(.Bits(3)) pulldown_58 (.out(CT_RF__MA));
  PullDown #(.Bits(5)) pulldown_59 (.out(CT_RF__RB));
  PullDown #(.Bits(3)) pulldown_60 (.out(CT_RF__MB));
  PullDown pulldown_61 (.out(CT_RF__PCSE));
  PullDown pulldown_62 (.out(CT_RF__PCJ));
  PullDown pulldown_63 (.out(CT_RF__PCR));
  PullDown #(.Bits(3)) pulldown_64 (.out(CT_RF__SCN));
  PullDown pulldown_65 (.out(CT_RF__SCD));
  PullDown #(.Bits(9)) pulldown_66 (.out(CT_ALU__CT));
  PullDown pulldown_67 (.out(CT_ALU__M));
  PullDown pulldown_68 (.out(CT_ALU__M2));
  PullDown pulldown_69 (.out(CT_BUS__IAR));
  PullDown pulldown_70 (.out(CT_BUS__IAG));
  PullDown pulldown_71 (.out(CT_BUS__IDR));
  PullDown pulldown_72 (.out(CT_BUS__IDM));
  PullDown pulldown_73 (.out(CT_BUS__DAR));
  PullDown pulldown_74 (.out(CT_BUS__DAM));
  PullDown pulldown_75 (.out(CT_BUS__DAG));
  PullDown pulldown_76 (.out(CT_BUS__DDR));
  PullDown pulldown_77 (.out(CT_BUS__DDG));
  PullDown pulldown_78 (.out(I_LD));
  PullDown pulldown_79 (.out(D_LD));
  PullDown pulldown_80 (.out(D_ST));
  PullDown #(.Bits(2)) pulldown_81 (.out(D_MD));
  PullDown pulldown_82 (.out(CT_MVR));
  and and_189 (and_189_out, JPU_BTB__pred[0], JPU_BTB__pred[1]);
  and and_190 (and_190_out, JPU_BTB__pred[0], JPU_JP);
  and and_191 (and_191_out, JPU_BTB__pred[1], JPU_JP);
  and and_192 (and_192_out, not_36_out, not_35_out, JPU_BTB__pred[1]);
  and and_193 (and_193_out, not_36_out, not_35_out, JPU_JP);
  and and_194 (and_194_out, JPU_BTB__pred[1], not_35_out, JPU_JP);
  D_FF #(.Bits(4)) d_ff_22 (.D(priorityencoder_1_num), .C(C_ct), .Q(RET_INST));  // open: nQ
  D_FF d_ff_23 (.D(bitselector_1_out), .C(C_ct), .Q(RET_EPOCH));  // open: nQ
  and and_195 (and_195_out, ~and_199_out, and_188_out);  // And
  inst_comp inst_comp_11 (.A_id(RET_INST), .A_ep(RET_EPOCH), .B_id(clr_id), .B_ep(clr_ep), .A_new(inst_comp_11_a_new));
  and and_196 (and_196_out, ~and_199_out, and_188_out);  // And
  inst_comp inst_comp_12 (
    .A_id(priorityencoder_1_num), .A_ep(bitselector_1_out), .B_id(clr_id), .B_ep(clr_ep),
    .A_new(inst_comp_12_a_new));
  PullDown pulldown_83 (.out(CT_TRAP__LD));
  PullDown pulldown_84 (.out(CT_KILL));
  data_select_4 data_select_4_1 (
    .D1_sel(store_controller_1_d1_sel), .D2_sel(store_controller_1_d2_sel), .in1(ALU_A_INST),
    .in2(ALU_B_INST), .in3(DIR_INST), .in4(LDB_B__INST), .in5(4'b0000), .in6(4'b0000), .in7(4'b0000),
    .in8(4'b0000), .out1(ROB_GEN_INSTA), .out2(ROB_GEN_INSTB));
  and and_197 (and_197_out[6], MB_free, JPU_free);
  or or_67 (JPU_pred[1], and_189_out, and_190_out, and_191_out, BTB_override);
  or or_68 (JPU_pred[0], and_192_out, and_193_out, and_194_out);
  not not_37 (JPU_free, and_195_out);
  and and_198 (and_198_out, inst_comp_11_a_new, clr);
  D_FF d_ff_24 (.D(and_196_out), .C(C_ct), .Q(d_ff_24_q));  // open: nQ
  and and_199 (and_199_out, inst_comp_12_a_new, clr);
  PullDown pulldown_85 (.out(ex_nop));
  PullDown pulldown_86 (.out(CT_ISS__HALT));
  Comparator #(.Bits(32)) comparator_20 (.a(JPU_ADDR), .b(JPU_BTB__tar), .eq(comparator_20_eq));  // open: gt, lt
  and and_200 (and_200_out, ~and_198_out, d_ff_24_q);  // And
  PullDown pulldown_87 (.out(issue));
  PullDown pulldown_88 (.out(CT_ISS__URA));
  PullDown pulldown_89 (.out(CT_ISS__URB));
  PullDown #(.Bits(5)) pulldown_90 (.out(CT_ISS__RA));
  PullDown #(.Bits(5)) pulldown_91 (.out(CT_ISS__RB));
  PullDown pulldown_92 (.out(CT_ISS__UMM));
  PullDown pulldown_93 (.out(CT_ISS__UFL));
  PullDown pulldown_94 (.out(CT_ISS__ORC));
  PullDown #(.Bits(5)) pulldown_95 (.out(CT_ISS__RC));
  PullDown pulldown_96 (.out(CT_ISS__OSC));
  PullDown pulldown_97 (.out(CT_ISS__OFL));
  PullDown pulldown_98 (.out(CT_ROB__EX__E));
  PullDown pulldown_99 (.out(CT_ROB__ST__E));
  PullDown #(.Bits(3)) pulldown_100 (.out(CT_SP__MOF));
  PullDown pulldown_101 (.out(CT_BUS__DDM));
  PullDown pulldown_102 (.out(CT_RF__PCH));
  PullDown pulldown_103 (.out(\wait ));
  nand nand_12 (nand_12_out, JPU_BTB__V, comparator_20_eq);
  and and_201 (and_201_out, JPU_MISS, JPU_BTB__V, comparator_20_eq);
  and and_202 (Fl_JPU, or_69_out, JPU_BTB__ST);
  Comparator #(.Bits(3)) comparator_21 (
    .a(store_controller_1_d1_sel), .b(3'b010), .eq(comparator_21_eq));  // open: gt, lt
  Comparator #(.Bits(3)) comparator_22 (
    .a(store_controller_1_d2_sel), .b(3'b010), .eq(comparator_22_eq));  // open: gt, lt
  D_FF #(.Bits(8)) d_ff_25 (
    .D({JPU_free, and_197_out[6], 1'b0, TRAP_free, MB_free, DIR_free, ALU_free, 1'b1}), .C(C_ct), .Q(FU_free));  // open: nQ
  assign CT_JPU__LD = and_200_out ? 1'b1 : 1'bz;  // Driver driver_208
  assign JPU_RET = and_200_out ? 1'b1 : 1'bz;  // Driver driver_209
  and and_203 (ROB_GEN_EX1, comparator_21_eq, DIR_EX);
  and and_204 (ROB_GEN_EX2, comparator_22_eq, DIR_EX);
  and and_205 (BTB_override, JPU_JP, nand_12_out);
  and and_206 (and_206_out, nand_12_out, JPU_BTB__J);
  or or_69 (or_69_out, and_201_out, and_206_out, BTB_override);
  assign CT_RF__PCSE = Fl_JPU ? 1'b1 : 1'bz;  // Driver driver_210
  assign CT_RF__PCJ = Fl_JPU ? 1'b1 : 1'bz;  // Driver driver_211
  PullDown pulldown_104 (.out(CT_RF__SCSRE));
  PullDown pulldown_105 (.out(CT_RF__SCSE));
  PullDown pulldown_106 (.out(CT_RF__SCSS));
  PullDown pulldown_107 (.out(CT_JPU__JP));
  PullDown pulldown_108 (.out(JPU_A__ST));
  PullDown pulldown_109 (.out(CT_MB__OFFM));
  PullDown pulldown_110 (.out(JPU_BTB__ST));
  PullDown pulldown_111 (.out(CT_JPU__LD));
  PullDown pulldown_112 (.out(CT_FU__MF));
  PullDown pulldown_113 (.out(CT_CALL__LD));
  PullDown pulldown_114 (.out(CT_RET__LD));
  PullDown pulldown_115 (.out(JPU_RET));
  PullDown pulldown_116 (.out(JPU_free));
  PullDown pulldown_117 (.out(JPU_CALL));
  PullDown pulldown_118 (.out(CT_CALLM));

  assign CSH_mode = 2'b00;
  assign CSH_run = 1'b0;
  assign INT_str = 1'b0;
  assign MMU_base = {32{1'b0}};
  assign MMU_dis = 1'b0;
  assign MMU_en = 1'b0;

  // Other names for the same wires on the sheet: disp_32[31:0] = {byte_D0, byte_D1, byte_D2, byte_D3};
  //   imm16_2[15:0] = {byte_D2, byte_D3}; FU_CLR[2:0] = {DIR_CLR, ALU_B_CLR, ALU_A_CLR}; ALU_A_WR[2:0] = ALU_A_RM;
  //   ALU_B_WR[2:0] = ALU_B_RM; BTB_packet[2] = BTB_JP; BTB_pred[1:0] = BTB_packet[4:3];
  //   BTB_tar[31:0] = BTB_packet[36:5]; BTB_V = BTB_packet[1]; C_i = C_dt; Fl_INT__EP = com2_ep;
  //   Fl_INT__INST[3:0] = com2_inst; CT_RF__SCAS = CT_RF__SCAE; fl_i[8] = FL[14]; int_proc = FL[14]; trap = FL[15];
  //   FU_D__V[2:0] = {DIR_V, ALU_B_VD, ALU_A_VD}; LDB_B__V = FU_D__V[3]; FU_F__V[1:0] = {ALU_B_VF, ALU_A_VF};
  //   TRAP_VI = FU_I__V[0]; issue_32[31:0] = {byte_I0, byte_I1, byte_I2, byte_I3};
  //   JPU_BTBPK[36:1] = {JPU_BTB__tar, JPU_BTB__pred, JPU_BTB__J, JPU_BTB__V}; JPU_EN = JPU_BTB__ST;
  //   JPU_ST = JPU_BTB__ST; Fl_INT = INT_out; run_int = INT_out; scs_i[31:0] = ISC_sc; TRAP_CLR = FU_CLR[4]

  // Notes on the sheet:
  //   D_MD: 0:32
  //   1:16
  //   2:8
  //   3:u.u
  //   I_valid: default 1
  //   D_accept: default 1
  //   C: Hz: 4096
  //   tests
  //   decode circuit
  //   IO pins
  //   primeary signals
  //   pipeline controller
  //   kernal mode system
  //   interrupt system
  //   ext system
  //   syscall
  //   inst id manager
  //   contents of rom_1 (hex, n*v repeats v):
  //   39,38,38,37,a,38,37,35,36,a
  //   ALU
  //   register
  //   stack
  //   RAM
  //   register system
  //   ROB
  //   program counter controller
  //   bus system
  //   data bus ctrl
  //   trap
  //   jump
  //   call
  //   return
  //   wait/halt
  //   block
  //   exld/st
  //   stack circuit
  //   ALU system
  //   dir circuit
  //   load/store circuit
  //   issue circuit
  //   flag circuit
  //   FU aribiter
  //   jmp circuit
  //   return unit
  //   control bus
endmodule
