// Digital circuit load-buffer.dig as structural Verilog
module load_buffer (
  input  C,
  input  [3:0] inst,
  input  [3:0] com1_id,
  input  [3:0] com2_id,
  input  com1,
  input  com2,
  input  st_ep,
  input  [3:0] st_id,
  input  epoch,
  input  [31:0] st_addr,
  input  W_id,
  input  LD,
  input  [31:0] st_data,
  input  [3:0] inst_WD,
  input  [31:0] D,
  input  W_a,
  input  [3:0] inst_WA,
  input  [31:0] A,
  input  W_d,
  input  LDB,
  input  [1:0] MD,
  input  st,
  output [31:0] D_O,
  output V,
  output full,
  output M_V,
  output [31:0] M_A,
  output fl,
  output [3:0] M_id,
  output M_ep,
  output [3:0] id_O,
  output [1:0] M_MD,
  output fl_ep,
  output [3:0] fl_id
);

  wire and_1_out, and_2_out, and_6_out, and_7_out, and_8_out, and_9_out, and_10_out, and_11_out, and_14_out,
       and_15_out, and_21_out, and_22_out, and_26_out, and_27_out, and_30_out, and_31_out, and_35_out,
       and_36_out, comparator_1_eq, comparator_2_eq, comparator_3_eq, comparator_4_eq, comparator_5_eq,
       comparator_6_gt, comparator_6_lt, comparator_7_eq, comparator_8_eq, comparator_9_eq, comparator_10_eq,
       comparator_11_eq, comparator_12_gt, comparator_12_lt, comparator_13_eq, comparator_14_eq,
       comparator_15_eq, comparator_16_eq, comparator_17_eq, comparator_18_gt, comparator_18_lt,
       comparator_19_eq, comparator_20_eq, comparator_21_eq, comparator_22_eq, comparator_23_eq,
       comparator_24_gt, comparator_24_lt, ld_V, M1_AE, M1_AV, M1_CMP, M1_DE, M1_DV, M1_epoch, M1_IE,
       M1_SEL__A, M1_SEL__D, M1_VO, M2_AE, M2_AV, M2_CMP, M2_DE, M2_DV, M2_epoch, M2_IE, M2_SEL__A,
       M2_SEL__D, M2_VO, M3_AE, M3_AV, M3_CMP, M3_DE, M3_DV, M3_epoch, M3_IE, M3_SEL__A, M3_SEL__D, M3_VO,
       M4_AE, M4_AV, M4_CMP, M4_DE, M4_DV, M4_epoch, M4_IE, M4_SEL__A, M4_SEL__D, M4_VO, multiplexer_15_out,
       multiplexer_17_out, multiplexer_19_out, multiplexer_21_out, or_3_out, or_4_out, or_5_out, or_6_out,
       priorityencoder_2_any, priorityencoder_3_any, priorityencoder_4_any, priorityencoder_6_any,
       priorityencoder_7_any, xor_1_out, xor_2_out, xor_3_out, xor_4_out;
  wire [1:0] empty_id, flush_sel, M1_MD, M2_MD, M3_MD, M4_MD, priorityencoder_1_num, priorityencoder_2_num,
       priorityencoder_4_num, priorityencoder_6_num, priorityencoder_7_num, register_2_q, register_4_q,
       register_5_q, register_6_q, register_9_q, register_10_q, register_14_q, register_16_q, sel_A, sel_D;
  wire [3:0] and_3_out, and_4_out, and_5_out, and_12_out, and_13_out, bitextender_1_out, bitextender_2_out,
       bitextender_3_out, bitselector_1_out, bitselector_2_out, M1_inst, M2_inst, M3_inst, M4_inst,
       multiplexer_4_out, multiplexer_5_out, not_1_out, not_3_out, not_4_out, or_1_out, or_2_out,
       priority_4_1_out1, priority_4_2_out1, register_1_q, register_3_q;
  wire [31:0] ld_O, M1_A, M1_D, M2_A, M2_D, M3_A, M3_D, M4_A, M4_D, multiplexer_14_out, multiplexer_16_out,
       multiplexer_18_out, multiplexer_20_out;

  PriorityEncoder #(.Selector_Bits(2)) priorityencoder_1 (
    .in0(and_4_out[0]), .in1(and_4_out[1]), .in2(and_4_out[2]), .in3(and_4_out[3]),
    .num(priorityencoder_1_num), .any(ld_V));
  Demultiplexer #(.Selector_Bits(2)) demultiplexer_1 (
    .sel(empty_id), .in(W_id), .out_0(M1_IE), .out_1(M2_IE), .out_2(M3_IE), .out_3(M4_IE));
  PriorityEncoder #(.Selector_Bits(2)) priorityencoder_2 (
    .in0(M1_SEL__A), .in1(M2_SEL__A), .in2(M3_SEL__A), .in3(M4_SEL__A), .num(priorityencoder_2_num),
    .any(priorityencoder_2_any));
  Multiplexer #(.Selector_Bits(2), .Bits(32)) multiplexer_1 (
    .sel(sel_A), .in_0(M1_A), .in_1(M2_A), .in_2(M3_A), .in_3(M4_A), .out(M_A));
  priority_4 priority_4_1 (
    .on(1'b1), .in1(and_12_out[0]), .in2(and_12_out[1]), .in3(and_12_out[2]), .in4(and_12_out[3]),
    .out1(priority_4_1_out1[3]), .out2(priority_4_1_out1[2]), .out3(priority_4_1_out1[1]),
    .out4(priority_4_1_out1[0]));  // open: v
  and and_1 (and_1_out, not_3_out[3], 1'b1);
  priority_4 priority_4_2 (
    .on(1'b1), .in1(and_13_out[0]), .in2(and_13_out[1]), .in3(and_13_out[2]), .in4(and_13_out[3]),
    .out1(priority_4_2_out1[3]), .out2(priority_4_2_out1[2]), .out3(priority_4_2_out1[1]),
    .out4(priority_4_2_out1[0]));  // open: v
  and and_2 (and_2_out, not_4_out[3], 1'b1);
  assign and_3_out = {M4_CMP, M3_CMP, M2_CMP, M1_CMP} & bitextender_1_out & {M4_DV, M3_DV, M2_DV, M1_DV};  // And and_3, 4 bits wide
  assign and_4_out = ~{M4_DV, M3_DV, M2_DV, M1_DV} & bitextender_1_out & {M4_CMP, M3_CMP, M2_CMP, M1_CMP};  // And and_4, 4 bits wide
  assign not_1_out = ~{M4_VO, M3_VO, M2_VO, M1_VO};  // Not not_1, 4 bits wide
  assign and_5_out = {M4_SEL__D, M3_SEL__D, M2_SEL__D, M1_SEL__D} & ~{M4_DV, M3_DV, M2_DV, M1_DV};  // And and_5, 4 bits wide
  Register register_1 (.D(and_1_out), .C(C), .en(or_1_out[3]), .Q(register_1_q[0]));
  BitSelector #(.Selector_Bits(2)) bitselector_1 (
    .in({M4_AV, M3_AV, M2_AV, M1_AV}), .sel(register_2_q), .out(bitselector_1_out[0]));
  Register #(.Bits(2)) register_2 (.D(empty_id), .C(C), .en(W_id), .Q(register_2_q));
  Register register_3 (.D(and_2_out), .C(C), .en(or_2_out[3]), .Q(register_3_q[0]));
  BitSelector #(.Selector_Bits(2)) bitselector_2 (
    .in({M4_DV, M3_DV, M2_DV, M1_DV}), .sel(register_4_q), .out(bitselector_2_out[0]));
  Register #(.Bits(2)) register_4 (.D(empty_id), .C(C), .en(W_id), .Q(register_4_q));
  PriorityEncoder #(.Selector_Bits(2)) priorityencoder_3 (
    .in0(not_1_out[0]), .in1(not_1_out[1]), .in2(not_1_out[2]), .in3(not_1_out[3]), .num(empty_id),
    .any(priorityencoder_3_any));
  and and_6 (and_6_out, W_a, priorityencoder_2_any);
  PriorityEncoder #(.Selector_Bits(2)) priorityencoder_4 (
    .in0(and_5_out[0]), .in1(and_5_out[1]), .in2(and_5_out[2]), .in3(and_5_out[3]),
    .num(priorityencoder_4_num), .any(priorityencoder_4_any));
  and and_7 (and_7_out, not_3_out[2], register_1_q[0]);
  Register #(.Bits(2)) register_5 (.D(register_2_q), .C(C), .en(W_id), .Q(register_5_q));
  and and_8 (and_8_out, not_4_out[2], register_3_q[0]);
  Register #(.Bits(2)) register_6 (.D(register_4_q), .C(C), .en(W_id), .Q(register_6_q));
  BitExtender #(.inputBits(1), .outputBits(4)) bitextender_1 (.in(st), .out(bitextender_1_out));
  PriorityEncoder #(.Selector_Bits(2)) priorityencoder_5 (
    .in0(and_3_out[0]), .in1(and_3_out[1]), .in2(and_3_out[2]), .in3(and_3_out[3]), .num(flush_sel), .any(fl));
  not not_2 (full, priorityencoder_3_any);
  Multiplexer #(.Selector_Bits(2), .Bits(32)) multiplexer_2 (
    .sel(sel_D), .in_0(M1_D), .in_1(M2_D), .in_2(M3_D), .in_3(M4_D), .out(D_O));
  Demultiplexer #(.Selector_Bits(2)) demultiplexer_2 (
    .sel(priorityencoder_2_num), .in(and_6_out), .out_0(M1_AE), .out_1(M2_AE), .out_2(M3_AE), .out_3(M4_AE));
  Multiplexer #(.Selector_Bits(2), .Bits(4)) multiplexer_3 (
    .sel(sel_A), .in_0(M1_inst), .in_1(M2_inst), .in_2(M3_inst), .in_3(M4_inst), .out(M_id));
  Multiplexer #(.Bits(4)) multiplexer_4 (
    .sel(W_id), .in_0(priority_4_1_out1), .in_1({1'b0, priority_4_1_out1[3:1]}), .out(multiplexer_4_out));
  Register register_7 (.D(and_7_out), .C(C), .en(or_1_out[2]), .Q(register_1_q[1]));
  BitSelector #(.Selector_Bits(2)) bitselector_3 (
    .in({M4_AV, M3_AV, M2_AV, M1_AV}), .sel(register_5_q), .out(bitselector_1_out[1]));
  Multiplexer #(.Bits(4)) multiplexer_5 (
    .sel(W_id), .in_0(priority_4_2_out1), .in_1({1'b0, priority_4_2_out1[3:1]}), .out(multiplexer_5_out));
  Register register_8 (.D(and_8_out), .C(C), .en(or_2_out[2]), .Q(register_3_q[1]));
  BitSelector #(.Selector_Bits(2)) bitselector_4 (
    .in({M4_DV, M3_DV, M2_DV, M1_DV}), .sel(register_6_q), .out(bitselector_2_out[1]));
  Multiplexer #(.Selector_Bits(2), .Bits(32)) multiplexer_6 (
    .sel(priorityencoder_1_num), .in_0(M1_D), .in_1(M2_D), .in_2(M3_D), .in_3(M4_D), .out(ld_O));
  and and_9 (and_9_out, W_d, priorityencoder_4_any);
  assign not_3_out = ~multiplexer_4_out;  // Not not_3, 4 bits wide
  BitExtender #(.inputBits(1), .outputBits(4)) bitextender_2 (.in(W_id), .out(bitextender_2_out));
  and and_10 (and_10_out, not_3_out[1], register_1_q[1]);
  Register #(.Bits(2)) register_9 (.D(register_5_q), .C(C), .en(W_id), .Q(register_9_q));
  assign not_4_out = ~multiplexer_5_out;  // Not not_4, 4 bits wide
  BitExtender #(.inputBits(1), .outputBits(4)) bitextender_3 (.in(W_id), .out(bitextender_3_out));
  and and_11 (and_11_out, not_4_out[1], register_3_q[1]);
  Register #(.Bits(2)) register_10 (.D(register_6_q), .C(C), .en(W_id), .Q(register_10_q));
  Multiplexer #(.Selector_Bits(2), .Bits(4)) multiplexer_7 (
    .sel(sel_D), .in_0(M1_inst), .in_1(M2_inst), .in_2(M3_inst), .in_3(M4_inst), .out(id_O));
  Demultiplexer #(.Selector_Bits(2)) demultiplexer_3 (
    .sel(priorityencoder_4_num), .in(and_9_out), .out_0(M1_DE), .out_1(M2_DE), .out_2(M3_DE), .out_3(M4_DE));
  Multiplexer #(.Selector_Bits(2)) multiplexer_8 (
    .sel(sel_A), .in_0(M1_epoch), .in_1(M2_epoch), .in_2(M3_epoch), .in_3(M4_epoch), .out(M_ep));
  assign or_1_out = priority_4_1_out1 | bitextender_2_out;  // Or or_1, 4 bits wide
  Register register_11 (.D(and_10_out), .C(C), .en(or_1_out[1]), .Q(register_1_q[2]));
  assign and_12_out = register_1_q & bitselector_1_out;  // And and_12, 4 bits wide
  BitSelector #(.Selector_Bits(2)) bitselector_5 (
    .in({M4_AV, M3_AV, M2_AV, M1_AV}), .sel(register_9_q), .out(bitselector_1_out[2]));
  assign or_2_out = priority_4_2_out1 | bitextender_3_out;  // Or or_2, 4 bits wide
  Register register_12 (.D(and_11_out), .C(C), .en(or_2_out[1]), .Q(register_3_q[2]));
  assign and_13_out = register_3_q & bitselector_2_out;  // And and_13, 4 bits wide
  BitSelector #(.Selector_Bits(2)) bitselector_6 (
    .in({M4_DV, M3_DV, M2_DV, M1_DV}), .sel(register_10_q), .out(bitselector_2_out[2]));
  Multiplexer #(.Selector_Bits(2)) multiplexer_9 (
    .sel(flush_sel), .in_0(M1_epoch), .in_1(M2_epoch), .in_2(M3_epoch), .in_3(M4_epoch), .out(fl_ep));
  Multiplexer #(.Selector_Bits(2), .Bits(4)) multiplexer_10 (
    .sel(flush_sel), .in_0(M1_inst), .in_1(M2_inst), .in_2(M3_inst), .in_3(M4_inst), .out(fl_id));
  Multiplexer #(.Selector_Bits(2), .Bits(2)) multiplexer_11 (
    .sel(sel_D), .in_0(M1_MD), .in_1(M2_MD), .in_2(M3_MD), .in_3(M4_MD), .out(M_MD));
  and and_14 (and_14_out, not_3_out[0], register_1_q[2]);
  Register register_13 (.D(and_14_out), .C(C), .en(or_1_out[0]), .Q(register_1_q[3]));
  Register #(.Bits(2)) register_14 (.D(register_9_q), .C(C), .en(W_id), .Q(register_14_q));
  and and_15 (and_15_out, not_4_out[0], register_3_q[2]);
  Register register_15 (.D(and_15_out), .C(C), .en(or_2_out[0]), .Q(register_3_q[3]));
  Register #(.Bits(2)) register_16 (.D(register_10_q), .C(C), .en(W_id), .Q(register_16_q));
  PriorityEncoder #(.Selector_Bits(2)) priorityencoder_6 (
    .in0(and_12_out[0]), .in1(and_12_out[1]), .in2(and_12_out[2]), .in3(and_12_out[3]),
    .num(priorityencoder_6_num), .any(priorityencoder_6_any));
  BitSelector #(.Selector_Bits(2)) bitselector_7 (
    .in({M4_AV, M3_AV, M2_AV, M1_AV}), .sel(register_14_q), .out(bitselector_1_out[3]));
  Multiplexer #(.Selector_Bits(2), .Bits(2)) multiplexer_12 (
    .sel(priorityencoder_6_num), .in_0(register_2_q), .in_1(register_5_q), .in_2(register_9_q),
    .in_3(register_14_q), .out(sel_A));
  PriorityEncoder #(.Selector_Bits(2)) priorityencoder_7 (
    .in0(and_13_out[0]), .in1(and_13_out[1]), .in2(and_13_out[2]), .in3(and_13_out[3]),
    .num(priorityencoder_7_num), .any(priorityencoder_7_any));
  BitSelector #(.Selector_Bits(2)) bitselector_8 (
    .in({M4_DV, M3_DV, M2_DV, M1_DV}), .sel(register_16_q), .out(bitselector_2_out[3]));
  Multiplexer #(.Selector_Bits(2), .Bits(2)) multiplexer_13 (
    .sel(priorityencoder_7_num), .in_0(register_4_q), .in_1(register_6_q), .in_2(register_10_q),
    .in_3(register_16_q), .out(sel_D));
  RS_FF rs_ff_1 (.S(M1_IE), .C(C), .R(or_3_out), .Q(M1_VO));  // open: nQ
  Comparator #(.Bits(32)) comparator_1 (.a(st_addr), .b(M1_A), .eq(comparator_1_eq));  // open: gt, lt
  Register #(.Bits(32)) register_17 (.D(A), .C(C), .en(M1_AE), .Q(M1_A));
  RS_FF rs_ff_2 (.S(M1_AE), .C(C), .R(or_3_out), .Q(M1_AV));  // open: nQ
  Register #(.Bits(2)) register_18 (.D(MD), .C(C), .en(M1_AE), .Q(M1_MD));
  Register #(.Bits(32)) register_19 (.D(multiplexer_14_out), .C(C), .en(M1_DE), .Q(M1_D));
  RS_FF rs_ff_3 (.S(M1_DE), .C(C), .R(or_3_out), .Q(M1_DV));  // open: nQ
  Comparator #(.Bits(4)) comparator_2 (.a(M1_inst), .b(inst_WA), .eq(comparator_2_eq));  // open: gt, lt
  Comparator #(.Bits(4)) comparator_3 (.a(M1_inst), .b(inst_WD), .eq(comparator_3_eq));  // open: gt, lt
  Comparator #(.Bits(4)) comparator_4 (.a(M1_inst), .b(com1_id), .eq(comparator_4_eq));  // open: gt, lt
  Comparator #(.Bits(4)) comparator_5 (.a(M1_inst), .b(com2_id), .eq(comparator_5_eq));  // open: gt, lt
  Register #(.Bits(4)) register_20 (.D(inst), .C(C), .en(M1_IE), .Q(M1_inst));
  Register register_21 (.D(epoch), .C(C), .en(M1_IE), .Q(M1_epoch));
  Comparator #(.Bits(4)) comparator_6 (.a(M1_inst), .b(st_id), .gt(comparator_6_gt), .lt(comparator_6_lt));  // open: eq
  xor xor_1 (xor_1_out, M1_epoch, st_ep);
  and and_16 (M_V, priorityencoder_6_any, LD);
  and and_17 (V, priorityencoder_7_any, LDB);
  and and_18 (M1_CMP, M1_VO, comparator_1_eq, multiplexer_15_out);
  Multiplexer #(.Bits(32)) multiplexer_14 (.sel(M1_CMP), .in_0(D), .in_1(st_data), .out(multiplexer_14_out));
  and and_19 (M1_SEL__A, M1_VO, comparator_2_eq);
  and and_20 (M1_SEL__D, M1_VO, comparator_3_eq);
  or or_3 (or_3_out, and_22_out, and_21_out);
  and and_21 (and_21_out, comparator_4_eq, com1);
  and and_22 (and_22_out, comparator_5_eq, com2);
  Multiplexer multiplexer_15 (
    .sel(xor_1_out), .in_0(comparator_6_gt), .in_1(comparator_6_lt), .out(multiplexer_15_out));
  RS_FF rs_ff_4 (.S(M2_IE), .C(C), .R(or_4_out), .Q(M2_VO));  // open: nQ
  Comparator #(.Bits(32)) comparator_7 (.a(st_addr), .b(M2_A), .eq(comparator_7_eq));  // open: gt, lt
  Register #(.Bits(32)) register_22 (.D(A), .C(C), .en(M2_AE), .Q(M2_A));
  RS_FF rs_ff_5 (.S(M2_AE), .C(C), .R(or_4_out), .Q(M2_AV));  // open: nQ
  Register #(.Bits(2)) register_23 (.D(MD), .C(C), .en(M2_AE), .Q(M2_MD));
  Register #(.Bits(32)) register_24 (.D(multiplexer_16_out), .C(C), .en(M2_DE), .Q(M2_D));
  RS_FF rs_ff_6 (.S(M2_DE), .C(C), .R(or_4_out), .Q(M2_DV));  // open: nQ
  Comparator #(.Bits(4)) comparator_8 (.a(M2_inst), .b(inst_WA), .eq(comparator_8_eq));  // open: gt, lt
  Comparator #(.Bits(4)) comparator_9 (.a(M2_inst), .b(inst_WD), .eq(comparator_9_eq));  // open: gt, lt
  Comparator #(.Bits(4)) comparator_10 (.a(M2_inst), .b(com1_id), .eq(comparator_10_eq));  // open: gt, lt
  Comparator #(.Bits(4)) comparator_11 (.a(M2_inst), .b(com2_id), .eq(comparator_11_eq));  // open: gt, lt
  Register #(.Bits(4)) register_25 (.D(inst), .C(C), .en(M2_IE), .Q(M2_inst));
  Register register_26 (.D(epoch), .C(C), .en(M2_IE), .Q(M2_epoch));
  Comparator #(.Bits(4)) comparator_12 (
    .a(M2_inst), .b(st_id), .gt(comparator_12_gt), .lt(comparator_12_lt));  // open: eq
  xor xor_2 (xor_2_out, M2_epoch, st_ep);
  and and_23 (M2_CMP, M2_VO, comparator_7_eq, multiplexer_17_out);
  Multiplexer #(.Bits(32)) multiplexer_16 (.sel(M2_CMP), .in_0(D), .in_1(st_data), .out(multiplexer_16_out));
  and and_24 (M2_SEL__A, M2_VO, comparator_8_eq);
  and and_25 (M2_SEL__D, M2_VO, comparator_9_eq);
  or or_4 (or_4_out, and_27_out, and_26_out);
  and and_26 (and_26_out, comparator_10_eq, com1);
  and and_27 (and_27_out, comparator_11_eq, com2);
  Multiplexer multiplexer_17 (
    .sel(xor_2_out), .in_0(comparator_12_gt), .in_1(comparator_12_lt), .out(multiplexer_17_out));
  RS_FF rs_ff_7 (.S(M3_IE), .C(C), .R(or_5_out), .Q(M3_VO));  // open: nQ
  Comparator #(.Bits(32)) comparator_13 (.a(st_addr), .b(M3_A), .eq(comparator_13_eq));  // open: gt, lt
  Register #(.Bits(32)) register_27 (.D(A), .C(C), .en(M3_AE), .Q(M3_A));
  RS_FF rs_ff_8 (.S(M3_AE), .C(C), .R(or_5_out), .Q(M3_AV));  // open: nQ
  Register #(.Bits(2)) register_28 (.D(MD), .C(C), .en(M3_AE), .Q(M3_MD));
  Register #(.Bits(32)) register_29 (.D(multiplexer_18_out), .C(C), .en(M3_DE), .Q(M3_D));
  RS_FF rs_ff_9 (.S(M3_DE), .C(C), .R(or_5_out), .Q(M3_DV));  // open: nQ
  Comparator #(.Bits(4)) comparator_14 (.a(M3_inst), .b(inst_WA), .eq(comparator_14_eq));  // open: gt, lt
  and and_28 (M3_SEL__A, M3_VO, comparator_14_eq);
  Comparator #(.Bits(4)) comparator_15 (.a(M3_inst), .b(inst_WD), .eq(comparator_15_eq));  // open: gt, lt
  and and_29 (M3_SEL__D, M3_VO, comparator_15_eq);
  or or_5 (or_5_out, and_31_out, and_30_out);
  and and_30 (and_30_out, comparator_16_eq, com1);
  Comparator #(.Bits(4)) comparator_16 (.a(M3_inst), .b(com1_id), .eq(comparator_16_eq));  // open: gt, lt
  and and_31 (and_31_out, comparator_17_eq, com2);
  Comparator #(.Bits(4)) comparator_17 (.a(M3_inst), .b(com2_id), .eq(comparator_17_eq));  // open: gt, lt
  Register #(.Bits(4)) register_30 (.D(inst), .C(C), .en(M3_IE), .Q(M3_inst));
  Register register_31 (.D(epoch), .C(C), .en(M3_IE), .Q(M3_epoch));
  Comparator #(.Bits(4)) comparator_18 (
    .a(M3_inst), .b(st_id), .gt(comparator_18_gt), .lt(comparator_18_lt));  // open: eq
  xor xor_3 (xor_3_out, M3_epoch, st_ep);
  and and_32 (M3_CMP, M3_VO, comparator_13_eq, multiplexer_19_out);
  Multiplexer #(.Bits(32)) multiplexer_18 (.sel(M3_CMP), .in_0(D), .in_1(st_data), .out(multiplexer_18_out));
  Multiplexer multiplexer_19 (
    .sel(xor_3_out), .in_0(comparator_18_gt), .in_1(comparator_18_lt), .out(multiplexer_19_out));
  RS_FF rs_ff_10 (.S(M4_IE), .C(C), .R(or_6_out), .Q(M4_VO));  // open: nQ
  Comparator #(.Bits(32)) comparator_19 (.a(st_addr), .b(M4_A), .eq(comparator_19_eq));  // open: gt, lt
  Register #(.Bits(32)) register_32 (.D(A), .C(C), .en(M4_AE), .Q(M4_A));
  RS_FF rs_ff_11 (.S(M4_AE), .C(C), .R(or_6_out), .Q(M4_AV));  // open: nQ
  Register #(.Bits(2)) register_33 (.D(MD), .C(C), .en(M4_AE), .Q(M4_MD));
  Multiplexer #(.Bits(32)) multiplexer_20 (.sel(M4_CMP), .in_0(D), .in_1(st_data), .out(multiplexer_20_out));
  Register #(.Bits(32)) register_34 (.D(multiplexer_20_out), .C(C), .en(M4_DE), .Q(M4_D));
  RS_FF rs_ff_12 (.S(M4_DE), .C(C), .R(or_6_out), .Q(M4_DV));  // open: nQ
  Comparator #(.Bits(4)) comparator_20 (.a(M4_inst), .b(inst_WA), .eq(comparator_20_eq));  // open: gt, lt
  and and_33 (M4_SEL__A, M4_VO, comparator_20_eq);
  Comparator #(.Bits(4)) comparator_21 (.a(M4_inst), .b(inst_WD), .eq(comparator_21_eq));  // open: gt, lt
  and and_34 (M4_SEL__D, M4_VO, comparator_21_eq);
  or or_6 (or_6_out, and_36_out, and_35_out);
  and and_35 (and_35_out, comparator_22_eq, com1);
  Comparator #(.Bits(4)) comparator_22 (.a(M4_inst), .b(com1_id), .eq(comparator_22_eq));  // open: gt, lt
  and and_36 (and_36_out, comparator_23_eq, com2);
  Comparator #(.Bits(4)) comparator_23 (.a(M4_inst), .b(com2_id), .eq(comparator_23_eq));  // open: gt, lt
  Register #(.Bits(4)) register_35 (.D(inst), .C(C), .en(M4_IE), .Q(M4_inst));
  Register register_36 (.D(epoch), .C(C), .en(M4_IE), .Q(M4_epoch));
  Comparator #(.Bits(4)) comparator_24 (
    .a(M4_inst), .b(st_id), .gt(comparator_24_gt), .lt(comparator_24_lt));  // open: eq
  xor xor_4 (xor_4_out, M4_epoch, st_ep);
  and and_37 (M4_CMP, M4_VO, comparator_19_eq, multiplexer_21_out);
  Multiplexer multiplexer_21 (
    .sel(xor_4_out), .in_0(comparator_24_gt), .in_1(comparator_24_lt), .out(multiplexer_21_out));

  // Other names for the same wires on the sheet: comp_addr[31:0] = st_addr; comp_ep = st_ep; comp_id[3:0] = st_id;
  //   flush = fl; flush_ep = fl_ep; flush_id[3:0] = fl_id; LDM = LD; MD_O[1:0] = M_MD
endmodule
